// Logisim project NumPrint2to10.circ as structural Verilog: 5 circuits, main circuit main
module main (
  input  in_1,
  input  in_2,
  input  in_3,
  input  in_4
);

  wire segment7_1_out_11, segment7_1_out_12, segment7_1_out_13, segment7_1_out_14, segment7_1_out_15,
       segment7_1_out_16, segment7_1_out_17, trans410_1_out_5, trans410_1_out_6, trans410_1_out_7,
       trans410_1_out_8, trans410_1_out_9, trans410_1_out_10, trans410_1_out_11, trans410_1_out_12,
       trans410_1_out_13, trans410_1_out_14;

  trans410 trans410_1 (
    .in_1(in_1), .in_2(in_2), .in_3(in_3), .in_4(in_4), .out_5(trans410_1_out_5), .out_6(trans410_1_out_6),
    .out_7(trans410_1_out_7), .out_8(trans410_1_out_8), .out_9(trans410_1_out_9), .out_10(trans410_1_out_10),
    .out_11(trans410_1_out_11), .out_12(trans410_1_out_12), .out_13(trans410_1_out_13),
    .out_14(trans410_1_out_14));
  segment7 segment7_1 (
    .in_1(trans410_1_out_5), .in_2(trans410_1_out_6), .in_3(trans410_1_out_7), .in_4(trans410_1_out_8),
    .in_5(trans410_1_out_9), .in_6(trans410_1_out_10), .in_7(trans410_1_out_11), .in_8(trans410_1_out_12),
    .in_9(trans410_1_out_13), .in_10(trans410_1_out_14), .out_11(segment7_1_out_11),
    .out_12(segment7_1_out_12), .out_13(segment7_1_out_13), .out_14(segment7_1_out_14),
    .out_15(segment7_1_out_15), .out_16(segment7_1_out_16), .out_17(segment7_1_out_17));
  _7_Segment_Display u_7_segment_display_1 (
    .g(segment7_1_out_17), .f(segment7_1_out_16), .a(segment7_1_out_11), .b(segment7_1_out_12),
    .e(segment7_1_out_15), .d(segment7_1_out_14), .c(segment7_1_out_13), .dp(1'b1));
endmodule

module Man_madeXNOR (
  input  in_1,
  input  in_2,
  output out_3
);

  wire transistor_1_out;

  Transistor transistor_1 (.in(1'b1), .out(transistor_1_out), .gate(in_1));
  Transistor #(.\type ("n")) transistor_2 (.in(1'b0), .out(transistor_1_out), .gate(in_1));
  Transistor #(.\type ("n")) transistor_3 (.in(in_1), .out(out_3), .gate(in_2));
  Transistor transistor_4 (.in(transistor_1_out), .out(out_3), .gate(in_2));
  Transistor #(.\type ("n")) transistor_5 (.in(in_2), .out(out_3), .gate(in_1));
  Transistor transistor_6 (.in(in_2), .out(out_3), .gate(transistor_1_out));
endmodule

module decoder38 (
  input  in_1,
  input  in_2,
  input  in_3,
  output out_4,
  output out_5,
  output out_6,
  output out_7,
  output out_8,
  output out_9,
  output out_10,
  output out_11
);

  wire and_1_out, and_2_out, and_3_out, and_4_out, not_1_out, not_2_out, not_3_out;

  not not_1 (not_1_out, in_1);
  not not_2 (not_2_out, in_2);
  not not_3 (not_3_out, in_3);
  and and_1 (and_1_out, not_1_out, not_2_out);
  and and_2 (and_2_out, not_1_out, in_2);
  and and_3 (and_3_out, not_2_out, in_1);
  and and_4 (and_4_out, in_1, in_2);
  and and_5 (out_4, and_1_out, not_3_out);
  and and_6 (out_5, and_3_out, not_3_out);
  and and_7 (out_6, and_2_out, not_3_out);
  and and_8 (out_7, and_4_out, not_3_out);
  and and_9 (out_8, and_1_out, in_3);
  and and_10 (out_9, and_3_out, in_3);
  and and_11 (out_10, and_2_out, in_3);
  and and_12 (out_11, and_4_out, in_3);
endmodule

module trans410 (
  input  in_1,
  input  in_2,
  input  in_3,
  input  in_4,
  output out_5,
  output out_6,
  output out_7,
  output out_8,
  output out_9,
  output out_10,
  output out_11,
  output out_12,
  output out_13,
  output out_14
);

  wire decoder38_1_out_4, decoder38_1_out_5, not_1_out, not_2_out;

  decoder38 decoder38_1 (
    .in_1(in_1), .in_2(in_2), .in_3(in_3), .out_4(decoder38_1_out_4), .out_5(decoder38_1_out_5),
    .out_6(out_7), .out_7(out_8), .out_8(out_9), .out_9(out_10), .out_10(out_11), .out_11(out_12));
  not not_1 (not_1_out, decoder38_1_out_5);
  and and_1 (out_13, in_4, not_1_out);
  and and_2 (out_14, decoder38_1_out_5, in_4);
  and and_3 (out_5, not_2_out, decoder38_1_out_4);
  and and_4 (out_6, decoder38_1_out_5, not_2_out);
  not not_2 (not_2_out, in_4);
endmodule

module segment7 (
  input  in_1,
  input  in_2,
  input  in_3,
  input  in_4,
  input  in_5,
  input  in_6,
  input  in_7,
  input  in_8,
  input  in_9,
  input  in_10,
  output out_11,
  output out_12,
  output out_13,
  output out_14,
  output out_15,
  output out_16,
  output out_17
);

  or or_1 (out_11, in_1, in_3, in_4, in_6, in_7, in_8, in_9, in_10);
  or or_2 (out_12, in_1, in_3, in_4, in_5, in_8, in_9, in_10, in_2);
  or or_3 (out_13, in_1, in_2, in_4, in_5, in_6, in_7, in_8, in_9, in_10);
  or or_4 (out_14, in_1, in_3, in_4, in_6, in_7, in_9, in_10);
  or or_5 (out_15, in_1, in_3, in_7, in_9);
  or or_6 (out_16, in_1, in_5, in_6, in_7, in_9, in_10);
  or or_7 (out_17, in_3, in_4, in_5, in_6, in_7, in_9, in_10);
endmodule
