// Logisim project Self_multiplexer.circ as structural Verilog
module decoder12 (
  input  in_1,
  output out_2,
  output out_3
);

  not not_1 (out_2, in_1);

  assign out_3 = in_1;
endmodule

module segment716 (
  input  in_1,
  input  in_2,
  input  in_3,
  input  in_4,
  input  in_5,
  input  in_6,
  input  in_7,
  input  in_8,
  input  in_9,
  input  in_10,
  input  in_11,
  input  in_12,
  input  in_13,
  input  in_14,
  input  in_15,
  input  in_16,
  output out_17,
  output out_18,
  output out_19,
  output out_20,
  output out_21,
  output out_22,
  output out_23
);

  wire segment710_1_out_11, segment710_1_out_12, segment710_1_out_13, segment710_1_out_14,
       segment710_1_out_15, segment710_1_out_16, segment710_1_out_17;

  segment710 segment710_1 (
    .in_1(in_1), .in_2(in_2), .in_3(in_3), .in_4(in_4), .in_5(in_5), .in_6(in_6), .in_7(in_7), .in_8(in_8),
    .in_9(in_9), .in_10(in_10), .out_11(segment710_1_out_11), .out_12(segment710_1_out_12),
    .out_13(segment710_1_out_13), .out_14(segment710_1_out_14), .out_15(segment710_1_out_15),
    .out_16(segment710_1_out_16), .out_17(segment710_1_out_17));
  or or_1 (out_17, segment710_1_out_11, in_11, in_13, in_15, in_16);
  or or_2 (out_18, segment710_1_out_12, in_11, in_14);
  or or_3 (out_19, in_11, segment710_1_out_13, in_12, in_14);
  or or_4 (out_20, in_12, segment710_1_out_14, in_13, in_14, in_15);
  or or_5 (out_21, in_16, in_13, segment710_1_out_15, in_11, in_14, in_12, in_15);
  or or_6 (out_22, in_13, segment710_1_out_16, in_11, in_12, in_15, in_16);
  or or_7 (out_23, segment710_1_out_17, in_11, in_12, in_14, in_15, in_16);
endmodule

module segment710 (
  input  in_1,
  input  in_2,
  input  in_3,
  input  in_4,
  input  in_5,
  input  in_6,
  input  in_7,
  input  in_8,
  input  in_9,
  input  in_10,
  output out_11,
  output out_12,
  output out_13,
  output out_14,
  output out_15,
  output out_16,
  output out_17
);

  or or_1 (out_11, in_1, in_3, in_4, in_6, in_7, in_8, in_9, in_10);
  or or_2 (out_12, in_1, in_3, in_4, in_5, in_8, in_9, in_10, in_2);
  or or_3 (out_13, in_1, in_2, in_4, in_5, in_6, in_7, in_8, in_9, in_10);
  or or_4 (out_14, in_1, in_3, in_4, in_6, in_7, in_9, in_10);
  or or_5 (out_15, in_1, in_3, in_7, in_9);
  or or_6 (out_16, in_1, in_5, in_6, in_7, in_9, in_10);
  or or_7 (out_17, in_3, in_4, in_5, in_6, in_7, in_9, in_10);
endmodule

module Multiplexer12 (
  input  in_1,
  input  in_2,
  input  in_3,
  output out_4
);

  wire and_1_out, and_2_out, decoder12_1_out_2, decoder12_1_out_3;

  decoder12 decoder12_1 (.in_1(in_1), .out_2(decoder12_1_out_2), .out_3(decoder12_1_out_3));
  and and_1 (and_1_out, in_2, decoder12_1_out_2);
  and and_2 (and_2_out, decoder12_1_out_3, in_3);
  or or_1 (out_4, and_1_out, and_2_out);
endmodule

module Multiplexer34 (
  input  in_1,
  input  in_2,
  input  in_3,
  input  in_4,
  input  in_5,
  input  in_6,
  input  in_7,
  input  in_8,
  input  in_9,
  input  in_10,
  input  in_11,
  input  in_12,
  input  in_13,
  input  in_14,
  output out_15,
  output out_16,
  output out_17
);

  wire and_1_out, and_2_out, and_3_out, and_4_out, and_5_out, and_6_out, and_7_out, and_8_out, and_9_out,
       and_10_out, and_11_out, and_12_out, decoder24_1_out_3, decoder24_1_out_4, decoder24_1_out_5,
       decoder24_1_out_6;

  decoder24 decoder24_1 (
    .in_1(in_1), .in_2(in_2), .out_3(decoder24_1_out_3), .out_4(decoder24_1_out_4),
    .out_5(decoder24_1_out_5), .out_6(decoder24_1_out_6));
  and and_1 (and_1_out, decoder24_1_out_3, in_3);
  and and_2 (and_2_out, decoder24_1_out_3, in_4);
  and and_3 (and_3_out, decoder24_1_out_3, in_5);
  and and_4 (and_4_out, decoder24_1_out_4, in_6);
  and and_5 (and_5_out, decoder24_1_out_4, in_7);
  and and_6 (and_6_out, decoder24_1_out_4, in_8);
  and and_7 (and_7_out, decoder24_1_out_5, in_9);
  and and_8 (and_8_out, decoder24_1_out_5, in_10);
  and and_9 (and_9_out, decoder24_1_out_5, in_11);
  and and_10 (and_10_out, decoder24_1_out_6, in_12);
  and and_11 (and_11_out, decoder24_1_out_6, in_13);
  and and_12 (and_12_out, decoder24_1_out_6, in_14);
  or or_1 (out_15, and_1_out, and_4_out, and_7_out, and_10_out);
  or or_2 (out_16, and_2_out, and_5_out, and_8_out, and_11_out);
  or or_3 (out_17, and_3_out, and_6_out, and_9_out, and_12_out);
endmodule

module decoder24 (
  input  in_1,
  input  in_2,
  output out_3,
  output out_4,
  output out_5,
  output out_6
);

  wire decoder12_1_out_2, decoder12_1_out_3, decoder12_2_out_2, decoder12_2_out_3;

  decoder12 decoder12_1 (.in_1(in_1), .out_2(decoder12_1_out_2), .out_3(decoder12_1_out_3));
  decoder12 decoder12_2 (.in_1(in_2), .out_2(decoder12_2_out_2), .out_3(decoder12_2_out_3));
  and and_1 (out_3, decoder12_2_out_2, decoder12_1_out_2);
  and and_2 (out_4, decoder12_1_out_3, decoder12_2_out_2);
  and and_3 (out_5, decoder12_1_out_2, decoder12_2_out_3);
  and and_4 (out_6, decoder12_1_out_3, decoder12_2_out_3);
endmodule
