// Logisim project Time_test.circ as structural Verilog: 1 circuit, main circuit main
module main (
  output out_1
);

  wire clock_1_out, clock_2_out;

  Clock #(.phaseOffset(1)) clock_1 (.out(clock_1_out));
  Clock clock_2 (.out(clock_2_out));
  or or_1 (out_1, clock_1_out, clock_2_out);
endmodule
