// Logisim project Timing_logic.circ as structural Verilog: 7 circuits, main circuit main
module main (
  input  in_1,
  input  in_2,
  input  in_3,
  input  in_4,
  input  in_5,
  input  in_6,
  input  in_7,
  input  in_8,
  output out_9,
  output out_10,
  output out_11,
  output out_12,
  output out_13,
  output out_14,
  output out_15,
  output out_16
);

  wire clock_1_out, clock_2_out, d_latch_2_out_5, not_1_out, not_2_out;

  Clock clock_1 (.out(clock_1_out));
  Clock clock_2 (.out(clock_2_out));
  not not_1 (not_1_out, in_1);
  not not_2 (not_2_out, in_3);
  D_flipflop d_flipflop_1 (.in_1(in_4), .in_2(in_5), .in_3(clock_1_out), .in_4(in_6), .out_5(out_13), .out_6(out_14));
  D_Latch d_latch_1 (.in_1(in_7), .in_2(clock_2_out), .in_3(in_8), .out_4(out_15), .out_5(out_16));
  SR_Latch sr_latch_1 (.in_1(not_1_out), .in_2(not_1_out), .out_3(out_9), .out_4(out_10));
  NSR_Latch nsr_latch_1 (.in_1(in_2), .in_2(in_2), .out_3(out_11), .out_4(out_12));
  D_Latch d_latch_2 (.in_1(d_latch_2_out_5), .in_2(1'b1), .in_3(not_2_out), .out_5(d_latch_2_out_5));  // open: out_4
endmodule

module wrong_CrossCoupledInverters (
  input  in_1,
  input  in_2,
  output out_3,
  output out_4
);

  not not_1 (in_2, in_1);
  not not_2 (in_1, in_2);

  assign out_3 = in_2;
  assign out_4 = in_1;
endmodule

module SR_Latch (
  input  in_1,
  input  in_2,
  output out_3,
  output out_4
);

  nor nor_1 (out_3, in_1, out_4);
  nor nor_2 (out_4, out_3, in_2);
endmodule

module D_Latch (
  input  in_1,
  input  in_2,
  input  in_3,
  output out_4,
  output out_5
);

  wire and_1_out, and_2_out, and_3_out, not_1_out, not_2_out, or_1_out;

  not not_1 (not_1_out, in_3);
  and and_1 (and_1_out, in_1, not_1_out);
  or or_1 (or_1_out, in_2, in_3);
  and and_2 (and_2_out, and_1_out, or_1_out);
  and and_3 (and_3_out, or_1_out, not_2_out);
  not not_2 (not_2_out, and_1_out);
  SR_Latch sr_latch_1 (.in_1(and_2_out), .in_2(and_3_out), .out_3(out_5), .out_4(out_4));
  // AND_Gate and_4 is placed but not wired
endmodule

module NSR_Latch (
  input  in_1,
  input  in_2,
  output out_3,
  output out_4
);

  nand nand_1 (out_3, in_1, out_4);
  nand nand_2 (out_4, out_3, in_2);
endmodule

module ND_Latch (
  input  in_1,
  input  in_2,
  output out_3,
  output out_4
);

  wire and_1_out, and_2_out, not_1_out;

  not not_1 (not_1_out, in_2);
  and and_1 (and_1_out, in_2, in_1);
  and and_2 (and_2_out, in_1, not_1_out);
  NSR_Latch nsr_latch_1 (.in_1(and_1_out), .in_2(and_2_out), .out_3(out_3), .out_4(out_4));
endmodule

module D_flipflop (
  input  in_1,
  input  in_2,
  input  in_3,
  input  in_4,
  output out_5,
  output out_6
);

  wire and_1_out, and_2_out, d_latch_1_out_4, not_1_out;

  and and_1 (and_1_out, in_2, in_3);
  and and_2 (and_2_out, in_1, in_2);
  not not_1 (not_1_out, and_1_out);
  D_Latch d_latch_1 (.in_1(and_2_out), .in_2(not_1_out), .in_3(in_4), .out_4(d_latch_1_out_4));  // open: out_5
  D_Latch d_latch_2 (.in_1(d_latch_1_out_4), .in_2(and_1_out), .in_3(in_4), .out_4(out_5), .out_5(out_6));
endmodule
