// Logisim project num.circ as structural Verilog
module comparator4 (
  input  in_1,
  input  in_2,
  input  in_3,
  input  in_4,
  input  in_5,
  input  in_6,
  input  in_7,
  input  in_8,
  output out_9
);

  wire xor_1_out, xor_2_out, xor_3_out, xor_4_out;

  xor xor_1 (xor_1_out, in_1, in_2);
  xor xor_2 (xor_2_out, in_3, in_4);
  xor xor_3 (xor_3_out, in_5, in_6);
  xor xor_4 (xor_4_out, in_7, in_8);
  nor nor_1 (out_9, xor_2_out, xor_3_out, xor_4_out);
endmodule

module add1 (
  input  in_1,
  input  in_2,
  input  in_3,
  output out_4,
  output out_5
);

  wire and_1_out, and_2_out, and_3_out, xor_1_out;

  and and_1 (and_1_out, in_2, in_1);
  and and_2 (and_2_out, in_3, in_1);
  and and_3 (and_3_out, in_2, in_3);
  xor xor_1 (xor_1_out, in_2, in_1);
  xor xor_2 (out_4, xor_1_out, in_3);
  or or_1 (out_5, and_1_out, and_2_out, and_3_out);
endmodule

module Half_add1 (
  input  in_1,
  input  in_2,
  output out_3,
  output out_4
);

  xor xor_1 (out_3, in_1, in_2);
  and and_1 (out_4, in_1, in_2);
endmodule

module Halfull_add1 (
  input  in_1,
  input  in_2,
  input  in_3,
  output out_4,
  output out_5
);

  wire half_add1_1_out_3, half_add1_1_out_4, half_add1_2_out_4;

  Half_add1 half_add1_1 (.in_1(in_2), .in_2(in_3), .out_3(half_add1_1_out_3), .out_4(half_add1_1_out_4));
  Half_add1 half_add1_2 (.in_1(in_1), .in_2(half_add1_1_out_3), .out_3(out_4), .out_4(half_add1_2_out_4));
  Half_add1 half_add1_3 (.in_1(half_add1_2_out_4), .in_2(half_add1_1_out_4), .out_3(out_5));  // open: out_4
endmodule

module add4 (
  input  in_1,
  input  in_2,
  input  in_3,
  input  in_4,
  input  in_5,
  input  in_6,
  input  in_7,
  input  in_8,
  output out_9,
  output out_10,
  output out_11,
  output out_12,
  output out_13
);

  wire halfull_add1_1_out_5, halfull_add1_2_out_5, halfull_add1_3_out_5;

  Halfull_add1 halfull_add1_1 (.in_2(in_1), .in_3(in_2), .out_4(out_9), .out_5(halfull_add1_1_out_5));  // open: in_1
  Halfull_add1 halfull_add1_2 (
    .in_1(halfull_add1_1_out_5), .in_2(in_3), .in_3(in_4), .out_4(out_10), .out_5(halfull_add1_2_out_5));
  Halfull_add1 halfull_add1_3 (
    .in_1(halfull_add1_2_out_5), .in_2(in_5), .in_3(in_6), .out_4(out_11), .out_5(halfull_add1_3_out_5));
  Halfull_add1 halfull_add1_4 (.in_1(halfull_add1_3_out_5), .in_2(in_7), .in_3(in_8), .out_4(out_12), .out_5(out_13));
endmodule
