// Logisim project switchable_segment.circ as structural Verilog: 17 circuits, main circuit main
module main (
  input  in_1,
  input  in_2,
  input  in_3,
  input  in_4,
  input  in_5
);

  wire and1to16_1_out_18, and1to16_1_out_19, and1to16_1_out_20, and1to16_1_out_21, and1to16_1_out_22,
       and1to16_1_out_23, and1to16_1_out_24, and1to16_1_out_25, and1to16_1_out_26, and1to16_1_out_27,
       and1to16_1_out_28, and1to16_1_out_29, and1to16_1_out_30, and1to16_1_out_31, and1to16_1_out_32,
       and1to16_1_out_33, and1to16_2_out_18, and1to16_2_out_19, and1to16_2_out_20, and1to16_2_out_21,
       and1to16_2_out_22, and1to16_2_out_23, and1to16_2_out_24, and1to16_2_out_25, and1to16_2_out_26,
       and1to16_2_out_27, decoder12_1_out_2, decoder12_1_out_3, decoder416_1_p5, decoder416_1_p6,
       decoder416_1_p7, decoder416_1_p8, decoder416_1_p9, decoder416_1_p10, decoder416_1_p11,
       decoder416_1_p12, decoder416_1_p13, decoder416_1_p14, decoder416_1_p15, decoder416_1_p16,
       decoder416_1_p17, decoder416_1_p18, decoder416_1_p19, decoder416_1_p20, segment710_1_out_11,
       segment710_1_out_12, segment710_1_out_13, segment710_1_out_14, segment710_1_out_15,
       segment710_1_out_16, segment710_1_out_17, segment716_1_out_17, segment716_1_out_18,
       segment716_1_out_19, segment716_1_out_20, segment716_1_out_21, segment716_1_out_22,
       segment716_1_out_23;

  // decoder416 decoder416_1: pin names not known; wires that end beside it: in_2, in_3, in_4, in_5, decoder416_1_p5, decoder416_1_p6, decoder416_1_p7, decoder416_1_p8, decoder416_1_p9, decoder416_1_p10, decoder416_1_p11, decoder416_1_p12, decoder416_1_p13, decoder416_1_p14, decoder416_1_p15, decoder416_1_p16, decoder416_1_p17, decoder416_1_p18, decoder416_1_p19, decoder416_1_p20
  decoder12 decoder12_1 (.in_1(in_1), .out_2(decoder12_1_out_2), .out_3(decoder12_1_out_3));
  and1to16 and1to16_1 (
    .in_1(decoder12_1_out_3), .in_2(decoder416_1_p5), .in_3(decoder416_1_p6), .in_4(decoder416_1_p7),
    .in_5(decoder416_1_p8), .in_6(decoder416_1_p9), .in_7(decoder416_1_p10), .in_8(decoder416_1_p11),
    .in_9(decoder416_1_p12), .in_10(decoder416_1_p13), .in_11(decoder416_1_p14), .in_12(decoder416_1_p15),
    .in_13(decoder416_1_p16), .in_14(decoder416_1_p17), .in_15(decoder416_1_p18), .in_16(decoder416_1_p19),
    .in_17(decoder416_1_p20), .out_18(and1to16_1_out_18), .out_19(and1to16_1_out_19),
    .out_20(and1to16_1_out_20), .out_21(and1to16_1_out_21), .out_22(and1to16_1_out_22),
    .out_23(and1to16_1_out_23), .out_24(and1to16_1_out_24), .out_25(and1to16_1_out_25),
    .out_26(and1to16_1_out_26), .out_27(and1to16_1_out_27), .out_28(and1to16_1_out_28),
    .out_29(and1to16_1_out_29), .out_30(and1to16_1_out_30), .out_31(and1to16_1_out_31),
    .out_32(and1to16_1_out_32), .out_33(and1to16_1_out_33));
  and1to16 and1to16_2 (
    .in_1(decoder12_1_out_2), .in_2(decoder416_1_p5), .in_3(decoder416_1_p6), .in_4(decoder416_1_p7),
    .in_5(decoder416_1_p8), .in_6(decoder416_1_p9), .in_7(decoder416_1_p10), .in_8(decoder416_1_p11),
    .in_9(decoder416_1_p12), .in_10(decoder416_1_p13), .in_11(decoder416_1_p14), .in_12(decoder416_1_p15),
    .in_13(decoder416_1_p16), .in_14(decoder416_1_p17), .in_15(decoder416_1_p18), .in_16(decoder416_1_p19),
    .in_17(decoder416_1_p20), .out_18(and1to16_2_out_18), .out_19(and1to16_2_out_19),
    .out_20(and1to16_2_out_20), .out_21(and1to16_2_out_21), .out_22(and1to16_2_out_22),
    .out_23(and1to16_2_out_23), .out_24(and1to16_2_out_24), .out_25(and1to16_2_out_25),
    .out_26(and1to16_2_out_26), .out_27(and1to16_2_out_27));  // open: out_28, out_29, out_30, out_31, out_32, out_33
  segment716 segment716_1 (
    .in_1(and1to16_1_out_18), .in_2(and1to16_1_out_19), .in_3(and1to16_1_out_20), .in_4(and1to16_1_out_21),
    .in_5(and1to16_1_out_22), .in_6(and1to16_1_out_23), .in_7(and1to16_1_out_24), .in_8(and1to16_1_out_25),
    .in_9(and1to16_1_out_26), .in_10(and1to16_1_out_27), .in_11(and1to16_1_out_28),
    .in_12(and1to16_1_out_29), .in_13(and1to16_1_out_30), .in_14(and1to16_1_out_31),
    .in_15(and1to16_1_out_32), .in_16(and1to16_1_out_33), .out_17(segment716_1_out_17),
    .out_18(segment716_1_out_18), .out_19(segment716_1_out_19), .out_20(segment716_1_out_20),
    .out_21(segment716_1_out_21), .out_22(segment716_1_out_22), .out_23(segment716_1_out_23));
  segment710 segment710_1 (
    .in_1(and1to16_2_out_18), .in_2(and1to16_2_out_19), .in_3(and1to16_2_out_20), .in_4(and1to16_2_out_21),
    .in_5(and1to16_2_out_22), .in_6(and1to16_2_out_23), .in_7(and1to16_2_out_24), .in_8(and1to16_2_out_25),
    .in_9(and1to16_2_out_26), .in_10(and1to16_2_out_27), .out_11(segment710_1_out_11),
    .out_12(segment710_1_out_12), .out_13(segment710_1_out_13), .out_14(segment710_1_out_14),
    .out_15(segment710_1_out_15), .out_16(segment710_1_out_16), .out_17(segment710_1_out_17));
  _7_Segment_Display u_7_segment_display_1 (
    .g(segment716_1_out_23), .f(segment716_1_out_22), .a(segment716_1_out_17), .b(segment716_1_out_18),
    .e(segment716_1_out_21), .d(segment716_1_out_20), .c(segment716_1_out_19), .dp(1'b1));
  _7_Segment_Display u_7_segment_display_2 (
    .g(segment716_1_out_23), .f(segment716_1_out_22), .a(segment716_1_out_17), .b(segment716_1_out_18),
    .e(segment716_1_out_21), .d(segment716_1_out_20), .c(segment716_1_out_19), .dp(1'b1));
  _7_Segment_Display u_7_segment_display_3 (
    .g(segment710_1_out_17), .f(segment710_1_out_16), .a(segment710_1_out_11), .b(segment710_1_out_12),
    .e(segment710_1_out_15), .d(segment710_1_out_14), .c(segment710_1_out_13), .dp(1'b1));
  _7_Segment_Display u_7_segment_display_4 (
    .g(segment710_1_out_17), .f(segment710_1_out_16), .a(segment710_1_out_11), .b(segment710_1_out_12),
    .e(segment710_1_out_15), .d(segment710_1_out_14), .c(segment710_1_out_13), .dp(1'b1));
endmodule

module encoder42 (
  input  in_1,
  input  in_2,
  input  in_3,
  input  in_4,
  output out_5,
  output out_6
);

  or or_1 (out_5, in_2, in_4);
  or or_2 (out_6, in_3, in_4);
endmodule

module encoder83 (
  input  in_1,
  input  in_2,
  input  in_3,
  input  in_4,
  input  in_5,
  input  in_6,
  input  in_7,
  input  in_8,
  output out_9,
  output out_10,
  output out_11
);

  wire encoder42_1_out_5, encoder42_1_out_6, encoder42_2_out_5, encoder42_2_out_6;

  encoder42 encoder42_1 (
    .in_1(in_1), .in_2(in_2), .in_3(in_3), .in_4(in_4), .out_5(encoder42_1_out_5), .out_6(encoder42_1_out_6));
  encoder42 encoder42_2 (
    .in_1(in_5), .in_2(in_6), .in_3(in_7), .in_4(in_8), .out_5(encoder42_2_out_5), .out_6(encoder42_2_out_6));
  or or_1 (out_9, encoder42_1_out_5, encoder42_2_out_5);
  or or_2 (out_10, encoder42_1_out_6, encoder42_2_out_6);
  or or_3 (out_11, in_5, in_6, in_7, in_8);
endmodule

module decoder12 (
  input  in_1,
  output out_2,
  output out_3
);

  not not_1 (out_2, in_1);

  assign out_3 = in_1;
endmodule

module decoder38 (
  input  in_1,
  input  in_2,
  input  in_3,
  output out_4,
  output out_5,
  output out_6,
  output out_7,
  output out_8,
  output out_9,
  output out_10,
  output out_11
);

  wire and_1_out, and_2_out, and_3_out, and_4_out, not_1_out, not_2_out, not_3_out;

  not not_1 (not_1_out, in_1);
  not not_2 (not_2_out, in_2);
  not not_3 (not_3_out, in_3);
  and and_1 (and_1_out, not_1_out, not_2_out);
  and and_2 (and_2_out, not_1_out, in_2);
  and and_3 (and_3_out, not_2_out, in_1);
  and and_4 (and_4_out, in_1, in_2);
  and and_5 (out_4, and_1_out, not_3_out);
  and and_6 (out_5, and_3_out, not_3_out);
  and and_7 (out_6, and_2_out, not_3_out);
  and and_8 (out_7, and_4_out, not_3_out);
  and and_9 (out_8, and_1_out, in_3);
  and and_10 (out_9, and_3_out, in_3);
  and and_11 (out_10, and_2_out, in_3);
  and and_12 (out_11, and_4_out, in_3);
endmodule

module segment716 (
  input  in_1,
  input  in_2,
  input  in_3,
  input  in_4,
  input  in_5,
  input  in_6,
  input  in_7,
  input  in_8,
  input  in_9,
  input  in_10,
  input  in_11,
  input  in_12,
  input  in_13,
  input  in_14,
  input  in_15,
  input  in_16,
  output out_17,
  output out_18,
  output out_19,
  output out_20,
  output out_21,
  output out_22,
  output out_23
);

  wire segment710_1_out_11, segment710_1_out_12, segment710_1_out_13, segment710_1_out_14,
       segment710_1_out_15, segment710_1_out_16, segment710_1_out_17;

  segment710 segment710_1 (
    .in_1(in_1), .in_2(in_2), .in_3(in_3), .in_4(in_4), .in_5(in_5), .in_6(in_6), .in_7(in_7), .in_8(in_8),
    .in_9(in_9), .in_10(in_10), .out_11(segment710_1_out_11), .out_12(segment710_1_out_12),
    .out_13(segment710_1_out_13), .out_14(segment710_1_out_14), .out_15(segment710_1_out_15),
    .out_16(segment710_1_out_16), .out_17(segment710_1_out_17));
  or or_1 (out_17, segment710_1_out_11, in_11, in_13, in_15, in_16);
  or or_2 (out_18, segment710_1_out_12, in_11, in_14);
  or or_3 (out_19, in_11, segment710_1_out_13, in_12, in_14);
  or or_4 (out_20, in_12, segment710_1_out_14, in_13, in_14, in_15);
  or or_5 (out_21, in_16, in_13, segment710_1_out_15, in_11, in_14, in_12, in_15);
  or or_6 (out_22, in_13, segment710_1_out_16, in_11, in_12, in_15, in_16);
  or or_7 (out_23, segment710_1_out_17, in_11, in_12, in_14, in_15, in_16);
endmodule

module segment710 (
  input  in_1,
  input  in_2,
  input  in_3,
  input  in_4,
  input  in_5,
  input  in_6,
  input  in_7,
  input  in_8,
  input  in_9,
  input  in_10,
  output out_11,
  output out_12,
  output out_13,
  output out_14,
  output out_15,
  output out_16,
  output out_17
);

  or or_1 (out_11, in_1, in_3, in_4, in_6, in_7, in_8, in_9, in_10);
  or or_2 (out_12, in_1, in_3, in_4, in_5, in_8, in_9, in_10, in_2);
  or or_3 (out_13, in_1, in_2, in_4, in_5, in_6, in_7, in_8, in_9, in_10);
  or or_4 (out_14, in_1, in_3, in_4, in_6, in_7, in_9, in_10);
  or or_5 (out_15, in_1, in_3, in_7, in_9);
  or or_6 (out_16, in_1, in_5, in_6, in_7, in_9, in_10);
  or or_7 (out_17, in_3, in_4, in_5, in_6, in_7, in_9, in_10);
endmodule

module decoder416 (
  input  in_1,
  input  in_2,
  input  in_3,
  input  in_4,
  output out_5,
  output out_6,
  output out_7,
  output out_8,
  output out_9,
  output out_10,
  output out_11,
  output out_12,
  output out_13,
  output out_14,
  output out_15,
  output out_16,
  output out_17,
  output out_18,
  output out_19,
  output out_20
);

  wire decoder38_1_out_4, decoder38_1_out_5, decoder38_1_out_6, decoder38_1_out_7, decoder38_1_out_8,
       decoder38_1_out_9, decoder38_1_out_10, decoder38_1_out_11, not_1_out;

  decoder38 decoder38_1 (
    .in_1(in_1), .in_2(in_2), .in_3(in_3), .out_4(decoder38_1_out_4), .out_5(decoder38_1_out_5),
    .out_6(decoder38_1_out_6), .out_7(decoder38_1_out_7), .out_8(decoder38_1_out_8),
    .out_9(decoder38_1_out_9), .out_10(decoder38_1_out_10), .out_11(decoder38_1_out_11));
  not not_1 (not_1_out, in_4);
  and and_1 (out_5, decoder38_1_out_4, not_1_out);
  and and_2 (out_6, decoder38_1_out_5, not_1_out);
  and and_3 (out_7, decoder38_1_out_6, not_1_out);
  and and_4 (out_8, decoder38_1_out_7, not_1_out);
  and and_5 (out_9, decoder38_1_out_8, not_1_out);
  and and_6 (out_10, decoder38_1_out_9, not_1_out);
  and and_7 (out_11, decoder38_1_out_10, not_1_out);
  and and_8 (out_12, decoder38_1_out_11, not_1_out);
  and and_9 (out_13, decoder38_1_out_4, in_4);
  and and_10 (out_14, decoder38_1_out_5, in_4);
  and and_11 (out_15, decoder38_1_out_6, in_4);
  and and_12 (out_16, decoder38_1_out_7, in_4);
  and and_13 (out_17, decoder38_1_out_8, in_4);
  and and_14 (out_18, decoder38_1_out_9, in_4);
  and and_15 (out_19, decoder38_1_out_10, in_4);
  and and_16 (out_20, decoder38_1_out_11, in_4);
endmodule

module encoder164 (
  input  in_1,
  input  in_2,
  input  in_3,
  input  in_4,
  input  in_5,
  input  in_6,
  input  in_7,
  input  in_8,
  input  in_9,
  input  in_10,
  input  in_11,
  input  in_12,
  input  in_13,
  input  in_14,
  input  in_15,
  input  in_16,
  output out_17,
  output out_18,
  output out_19,
  output out_20
);

  wire encoder83_1_out_9, encoder83_1_out_10, encoder83_1_out_11, encoder83_2_out_9, encoder83_2_out_10,
       encoder83_2_out_11;

  encoder83 encoder83_1 (
    .in_1(in_1), .in_2(in_2), .in_3(in_3), .in_4(in_4), .in_5(in_5), .in_6(in_6), .in_7(in_7), .in_8(in_8),
    .out_9(encoder83_1_out_9), .out_10(encoder83_1_out_10), .out_11(encoder83_1_out_11));
  encoder83 encoder83_2 (
    .in_1(in_9), .in_2(in_10), .in_3(in_11), .in_4(in_12), .in_5(in_13), .in_6(in_14), .in_7(in_15),
    .in_8(in_16), .out_9(encoder83_2_out_9), .out_10(encoder83_2_out_10), .out_11(encoder83_2_out_11));
  or or_1 (out_17, encoder83_1_out_9, encoder83_2_out_9);
  or or_2 (out_18, encoder83_1_out_10, encoder83_2_out_10);
  or or_3 (out_19, encoder83_1_out_11, encoder83_2_out_11);
  or or_4 (out_20, in_9, in_10, in_11, in_12, in_13, in_14, in_15, in_16);
endmodule

module prio_encoder42 (
  input  in_1,
  input  in_2,
  input  in_3,
  input  in_4,
  output out_5,
  output out_6
);

  wire and_1_out, not_1_out;

  not not_1 (not_1_out, in_3);
  or or_1 (out_6, in_3, in_4);
  and and_1 (and_1_out, in_2, not_1_out);
  or or_2 (out_5, and_1_out, in_4);
endmodule

module prio_encoder83 (
  input  in_1,
  input  in_2,
  input  in_3,
  input  in_4,
  input  in_5,
  input  in_6,
  input  in_7,
  input  in_8,
  output out_9,
  output out_10,
  output out_11
);

  wire and_1_out, and_2_out, not_1_out, prio_encoder42_1_out_5, prio_encoder42_1_out_6,
       prio_encoder42_2_out_5, prio_encoder42_2_out_6;

  prio_encoder42 prio_encoder42_1 (
    .in_1(in_1), .in_2(in_2), .in_3(in_3), .in_4(in_4), .out_5(prio_encoder42_1_out_5),
    .out_6(prio_encoder42_1_out_6));
  prio_encoder42 prio_encoder42_2 (
    .in_1(in_5), .in_2(in_6), .in_3(in_7), .in_4(in_8), .out_5(prio_encoder42_2_out_5),
    .out_6(prio_encoder42_2_out_6));
  and and_1 (and_1_out, not_1_out, prio_encoder42_1_out_5);
  and and_2 (and_2_out, not_1_out, prio_encoder42_1_out_6);
  not not_1 (not_1_out, out_11);
  or or_1 (out_9, and_1_out, prio_encoder42_2_out_5);
  or or_2 (out_10, and_2_out, prio_encoder42_2_out_6);
  or or_3 (out_11, in_5, in_6, in_7, in_8);
endmodule

module prio_encoder164 (
  input  in_1,
  input  in_2,
  input  in_3,
  input  in_4,
  input  in_5,
  input  in_6,
  input  in_7,
  input  in_8,
  input  in_9,
  input  in_10,
  input  in_11,
  input  in_12,
  input  in_13,
  input  in_14,
  input  in_15,
  input  in_16,
  output out_17,
  output out_18,
  output out_19,
  output out_20
);

  wire and_1_out, and_2_out, and_3_out, not_1_out, prio_encoder83_1_out_9, prio_encoder83_1_out_10,
       prio_encoder83_1_out_11, prio_encoder83_2_out_9, prio_encoder83_2_out_10, prio_encoder83_2_out_11;

  prio_encoder83 prio_encoder83_1 (
    .in_1(in_1), .in_2(in_2), .in_3(in_3), .in_4(in_4), .in_5(in_5), .in_6(in_6), .in_7(in_7), .in_8(in_8),
    .out_9(prio_encoder83_1_out_9), .out_10(prio_encoder83_1_out_10), .out_11(prio_encoder83_1_out_11));
  prio_encoder83 prio_encoder83_2 (
    .in_1(in_9), .in_2(in_10), .in_3(in_11), .in_4(in_12), .in_5(in_13), .in_6(in_14), .in_7(in_15),
    .in_8(in_16), .out_9(prio_encoder83_2_out_9), .out_10(prio_encoder83_2_out_10),
    .out_11(prio_encoder83_2_out_11));
  and and_1 (and_1_out, not_1_out, prio_encoder83_1_out_9);
  and and_2 (and_2_out, not_1_out, prio_encoder83_1_out_10);
  and and_3 (and_3_out, not_1_out, prio_encoder83_1_out_11);
  or or_1 (out_17, and_1_out, prio_encoder83_2_out_9);
  or or_2 (out_18, and_2_out, prio_encoder83_2_out_10);
  or or_3 (out_19, and_3_out, prio_encoder83_2_out_11);
  or or_4 (out_20, in_9, in_10, in_11, in_12, in_13, in_14, in_15, in_16);
  not not_1 (not_1_out, out_20);
endmodule

module Multiplexer12 (
  input  in_1,
  input  in_2,
  input  in_3,
  output out_4
);

  wire and_1_out, and_2_out, decoder12_1_out_2, decoder12_1_out_3;

  decoder12 decoder12_1 (.in_1(in_1), .out_2(decoder12_1_out_2), .out_3(decoder12_1_out_3));
  and and_1 (and_1_out, in_2, decoder12_1_out_2);
  and and_2 (and_2_out, decoder12_1_out_3, in_3);
  or or_1 (out_4, and_1_out, and_2_out);
endmodule

module Multiplexer34 (
  input  in_1,
  input  in_2,
  input  in_3,
  input  in_4,
  input  in_5,
  input  in_6,
  input  in_7,
  input  in_8,
  input  in_9,
  input  in_10,
  input  in_11,
  input  in_12,
  input  in_13,
  input  in_14,
  output out_15,
  output out_16,
  output out_17
);

  wire and_1_out, and_2_out, and_3_out, and_4_out, and_5_out, and_6_out, and_7_out, and_8_out, and_9_out,
       and_10_out, and_11_out, and_12_out, decoder24_1_out_3, decoder24_1_out_4, decoder24_1_out_5,
       decoder24_1_out_6;

  decoder24 decoder24_1 (
    .in_1(in_1), .in_2(in_2), .out_3(decoder24_1_out_3), .out_4(decoder24_1_out_4),
    .out_5(decoder24_1_out_5), .out_6(decoder24_1_out_6));
  and and_1 (and_1_out, decoder24_1_out_3, in_3);
  and and_2 (and_2_out, decoder24_1_out_3, in_4);
  and and_3 (and_3_out, decoder24_1_out_3, in_5);
  and and_4 (and_4_out, decoder24_1_out_4, in_6);
  and and_5 (and_5_out, decoder24_1_out_4, in_7);
  and and_6 (and_6_out, decoder24_1_out_4, in_8);
  and and_7 (and_7_out, decoder24_1_out_5, in_9);
  and and_8 (and_8_out, decoder24_1_out_5, in_10);
  and and_9 (and_9_out, decoder24_1_out_5, in_11);
  and and_10 (and_10_out, decoder24_1_out_6, in_12);
  and and_11 (and_11_out, decoder24_1_out_6, in_13);
  and and_12 (and_12_out, decoder24_1_out_6, in_14);
  or or_1 (out_15, and_1_out, and_4_out, and_7_out, and_10_out);
  or or_2 (out_16, and_2_out, and_5_out, and_8_out, and_11_out);
  or or_3 (out_17, and_3_out, and_6_out, and_9_out, and_12_out);
endmodule

module decoder24 (
  input  in_1,
  input  in_2,
  output out_3,
  output out_4,
  output out_5,
  output out_6
);

  wire decoder12_1_out_2, decoder12_1_out_3, decoder12_2_out_2, decoder12_2_out_3;

  decoder12 decoder12_1 (.in_1(in_1), .out_2(decoder12_1_out_2), .out_3(decoder12_1_out_3));
  decoder12 decoder12_2 (.in_1(in_2), .out_2(decoder12_2_out_2), .out_3(decoder12_2_out_3));
  and and_1 (out_3, decoder12_2_out_2, decoder12_1_out_2);
  and and_2 (out_4, decoder12_1_out_3, decoder12_2_out_2);
  and and_3 (out_5, decoder12_1_out_2, decoder12_2_out_3);
  and and_4 (out_6, decoder12_1_out_3, decoder12_2_out_3);
endmodule

module and1to4 (
  input  in_1,
  input  in_2,
  input  in_3,
  input  in_4,
  input  in_5,
  output out_6,
  output out_7,
  output out_8,
  output out_9
);

  and and_1 (out_6, in_1, in_2);
  and and_2 (out_7, in_1, in_3);
  and and_3 (out_8, in_1, in_4);
  and and_4 (out_9, in_1, in_5);
endmodule

module and1to16 (
  input  in_1,
  input  in_2,
  input  in_3,
  input  in_4,
  input  in_5,
  input  in_6,
  input  in_7,
  input  in_8,
  input  in_9,
  input  in_10,
  input  in_11,
  input  in_12,
  input  in_13,
  input  in_14,
  input  in_15,
  input  in_16,
  input  in_17,
  output out_18,
  output out_19,
  output out_20,
  output out_21,
  output out_22,
  output out_23,
  output out_24,
  output out_25,
  output out_26,
  output out_27,
  output out_28,
  output out_29,
  output out_30,
  output out_31,
  output out_32,
  output out_33
);

  and1to4 and1to4_1 (
    .in_1(in_1), .in_2(in_2), .in_3(in_3), .in_4(in_4), .in_5(in_5), .out_6(out_18), .out_7(out_19),
    .out_8(out_20), .out_9(out_21));
  and1to4 and1to4_2 (
    .in_1(in_1), .in_2(in_6), .in_3(in_7), .in_4(in_8), .in_5(in_9), .out_6(out_22), .out_7(out_23),
    .out_8(out_24), .out_9(out_25));
  and1to4 and1to4_3 (
    .in_1(in_1), .in_2(in_10), .in_3(in_11), .in_4(in_12), .in_5(in_13), .out_6(out_26), .out_7(out_27),
    .out_8(out_28), .out_9(out_29));
  and1to4 and1to4_4 (
    .in_1(in_1), .in_2(in_14), .in_3(in_15), .in_4(in_16), .in_5(in_17), .out_6(out_30), .out_7(out_31),
    .out_8(out_32), .out_9(out_33));
endmodule
