// Logisim project timer.circ as structural Verilog: 13 circuits, main circuit main
module main (
  input  in_1,
  input  in_2
);

  wire and_1_out, clock_1_out, comparator_1_eq, comparator_1_gt, comparator_2_eq, comparator_2_gt,
       comparator_3_eq, not_1_out, not_2_out, not_3_out, or_1_out, or_2_out;
  wire [7:0] adder_1_out, adder_2_out, adder_3_out, register_1_q, register_2_q, register_3_q;

  Clock clock_1 (.out(clock_1_out));
  and and_1 (and_1_out, not_1_out, clock_1_out, not_3_out, not_2_out);
  Register register_1 (.D(adder_1_out), .en(in_1), .clk(and_1_out), .Q(register_1_q), .clr(or_1_out));
  Register register_2 (.D(adder_2_out), .en(in_1), .clk(or_1_out), .Q(register_2_q), .clr(or_2_out));
  Register register_3 (.D(adder_3_out), .en(in_1), .clk(or_2_out), .Q(register_3_q), .clr(in_2));
  not not_1 (not_1_out, comparator_1_gt);
  not not_2 (not_2_out, comparator_2_gt);
  not not_3 (not_3_out, comparator_3_eq);
  Adder adder_1 (.a(register_1_q), .b(8'h1), .out(adder_1_out));  // open: cin, cout
  or or_1 (or_1_out, comparator_1_eq, in_2);
  Adder adder_2 (.a(register_2_q), .b(8'h1), .out(adder_2_out));  // open: cin, cout
  or or_2 (or_2_out, comparator_2_eq, in_2);
  Adder adder_3 (.a(register_3_q), .b(8'h1), .out(adder_3_out));  // open: cin, cout
  Comparator comparator_1 (.a(adder_1_out), .b(8'h3d), .gt(comparator_1_gt), .eq(comparator_1_eq));  // open: lt
  Comparator comparator_2 (.a(adder_2_out), .b(8'h3d), .gt(comparator_2_gt), .eq(comparator_2_eq));  // open: lt
  Comparator comparator_3 (.a(adder_3_out), .b(8'h19), .eq(comparator_3_eq));  // open: gt, lt
  _7_Segment_Display u_7_segment_display_1 ();  // open: g, f, a, b, e, d, c, dp
  // BCD_to_7_Segment_decoder bcd_to_7_segment_decoder_1: pin names not known
  // Binary_to_BCD_converter #(.binvalue(8)) binary_to_bcd_converter_1: pin names not known; wires that end beside it: register_1_q
  _7_Segment_Display u_7_segment_display_2 ();  // open: g, f, a, b, e, d, c, dp
  // BCD_to_7_Segment_decoder bcd_to_7_segment_decoder_2: pin names not known
  // Binary_to_BCD_converter #(.binvalue(8)) binary_to_bcd_converter_2: pin names not known; wires that end beside it: register_2_q
  _7_Segment_Display u_7_segment_display_3 ();  // open: g, f, a, b, e, d, c, dp
  // BCD_to_7_Segment_decoder bcd_to_7_segment_decoder_3: pin names not known
  // Binary_to_BCD_converter #(.binvalue(8)) binary_to_bcd_converter_3: pin names not known; wires that end beside it: register_3_q
  _7_Segment_Display u_7_segment_display_4 ();  // open: g, f, a, b, e, d, c, dp
  // BCD_to_7_Segment_decoder bcd_to_7_segment_decoder_4: pin names not known
  _7_Segment_Display u_7_segment_display_5 ();  // open: g, f, a, b, e, d, c, dp
  // BCD_to_7_Segment_decoder bcd_to_7_segment_decoder_5: pin names not known
  _7_Segment_Display u_7_segment_display_6 ();  // open: g, f, a, b, e, d, c, dp
  // BCD_to_7_Segment_decoder bcd_to_7_segment_decoder_6: pin names not known
endmodule

module vision_example (
  input  in_1,
  input  in_2,
  input  in_3,
  input  in_4,
  input  in_5,
  input  in_6,
  input  in_7
);

  _7_Segment_Display u_7_segment_display_1 (
    .g(in_7), .f(in_6), .a(in_1), .b(in_2), .e(in_5), .d(in_4), .c(in_3), .dp(1'b1));
endmodule

module encoder42 (
  input  in_1,
  input  in_2,
  input  in_3,
  input  in_4,
  output out_5,
  output out_6
);

  or or_1 (out_5, in_2, in_4);
  or or_2 (out_6, in_3, in_4);
endmodule

module encoder83 (
  input  in_1,
  input  in_2,
  input  in_3,
  input  in_4,
  input  in_5,
  input  in_6,
  input  in_7,
  input  in_8,
  output out_9,
  output out_10,
  output out_11
);

  wire encoder42_1_out_5, encoder42_1_out_6, encoder42_2_out_5, encoder42_2_out_6;

  encoder42 encoder42_1 (
    .in_1(in_1), .in_2(in_2), .in_3(in_3), .in_4(in_4), .out_5(encoder42_1_out_5), .out_6(encoder42_1_out_6));
  encoder42 encoder42_2 (
    .in_1(in_5), .in_2(in_6), .in_3(in_7), .in_4(in_8), .out_5(encoder42_2_out_5), .out_6(encoder42_2_out_6));
  or or_1 (out_9, encoder42_1_out_5, encoder42_2_out_5);
  or or_2 (out_10, encoder42_1_out_6, encoder42_2_out_6);
  or or_3 (out_11, in_5, in_6, in_7, in_8);
endmodule

module decoder12 (
  input  in_1,
  output out_2,
  output out_3
);

  not not_1 (out_2, in_1);

  assign out_3 = in_1;
endmodule

module decoder38 (
  input  in_1,
  input  in_2,
  input  in_3,
  output out_4,
  output out_5,
  output out_6,
  output out_7,
  output out_8,
  output out_9,
  output out_10,
  output out_11
);

  wire and_1_out, and_2_out, and_3_out, and_4_out, not_1_out, not_2_out, not_3_out;

  not not_1 (not_1_out, in_1);
  not not_2 (not_2_out, in_2);
  not not_3 (not_3_out, in_3);
  and and_1 (and_1_out, not_1_out, not_2_out);
  and and_2 (and_2_out, not_1_out, in_2);
  and and_3 (and_3_out, not_2_out, in_1);
  and and_4 (and_4_out, in_1, in_2);
  and and_5 (out_4, and_1_out, not_3_out);
  and and_6 (out_5, and_3_out, not_3_out);
  and and_7 (out_6, and_2_out, not_3_out);
  and and_8 (out_7, and_4_out, not_3_out);
  and and_9 (out_8, and_1_out, in_3);
  and and_10 (out_9, and_3_out, in_3);
  and and_11 (out_10, and_2_out, in_3);
  and and_12 (out_11, and_4_out, in_3);
endmodule

module segment716 (
  input  in_1,
  input  in_2,
  input  in_3,
  input  in_4,
  input  in_5,
  input  in_6,
  input  in_7,
  input  in_8,
  input  in_9,
  input  in_10,
  input  in_11,
  input  in_12,
  input  in_13,
  input  in_14,
  input  in_15,
  input  in_16,
  output out_17,
  output out_18,
  output out_19,
  output out_20,
  output out_21,
  output out_22,
  output out_23
);

  wire segment710_1_out_11, segment710_1_out_12, segment710_1_out_13, segment710_1_out_14,
       segment710_1_out_15, segment710_1_out_16, segment710_1_out_17;

  segment710 segment710_1 (
    .in_1(in_1), .in_2(in_2), .in_3(in_3), .in_4(in_4), .in_5(in_5), .in_6(in_6), .in_7(in_7), .in_8(in_8),
    .in_9(in_9), .in_10(in_10), .out_11(segment710_1_out_11), .out_12(segment710_1_out_12),
    .out_13(segment710_1_out_13), .out_14(segment710_1_out_14), .out_15(segment710_1_out_15),
    .out_16(segment710_1_out_16), .out_17(segment710_1_out_17));
  or or_1 (out_17, segment710_1_out_11, in_11, in_13, in_15, in_16);
  or or_2 (out_18, segment710_1_out_12, in_11, in_14);
  or or_3 (out_19, in_11, segment710_1_out_13, in_12, in_14);
  or or_4 (out_20, in_12, segment710_1_out_14, in_13, in_14, in_15);
  or or_5 (out_21, in_16, in_13, segment710_1_out_15, in_11, in_14, in_12, in_15);
  or or_6 (out_22, in_13, segment710_1_out_16, in_11, in_12, in_15, in_16);
  or or_7 (out_23, segment710_1_out_17, in_11, in_12, in_14, in_15, in_16);
endmodule

module segment710 (
  input  in_1,
  input  in_2,
  input  in_3,
  input  in_4,
  input  in_5,
  input  in_6,
  input  in_7,
  input  in_8,
  input  in_9,
  input  in_10,
  output out_11,
  output out_12,
  output out_13,
  output out_14,
  output out_15,
  output out_16,
  output out_17
);

  or or_1 (out_11, in_1, in_3, in_4, in_6, in_7, in_8, in_9, in_10);
  or or_2 (out_12, in_1, in_3, in_4, in_5, in_8, in_9, in_10, in_2);
  or or_3 (out_13, in_1, in_2, in_4, in_5, in_6, in_7, in_8, in_9, in_10);
  or or_4 (out_14, in_1, in_3, in_4, in_6, in_7, in_9, in_10);
  or or_5 (out_15, in_1, in_3, in_7, in_9);
  or or_6 (out_16, in_1, in_5, in_6, in_7, in_9, in_10);
  or or_7 (out_17, in_3, in_4, in_5, in_6, in_7, in_9, in_10);
endmodule

module decoder416 (
  input  in_1,
  input  in_2,
  input  in_3,
  input  in_4,
  output out_5,
  output out_6,
  output out_7,
  output out_8,
  output out_9,
  output out_10,
  output out_11,
  output out_12,
  output out_13,
  output out_14,
  output out_15,
  output out_16,
  output out_17,
  output out_18,
  output out_19,
  output out_20
);

  wire decoder38_1_out_4, decoder38_1_out_5, decoder38_1_out_6, decoder38_1_out_7, decoder38_1_out_8,
       decoder38_1_out_9, decoder38_1_out_10, decoder38_1_out_11, not_1_out;

  decoder38 decoder38_1 (
    .in_1(in_1), .in_2(in_2), .in_3(in_3), .out_4(decoder38_1_out_4), .out_5(decoder38_1_out_5),
    .out_6(decoder38_1_out_6), .out_7(decoder38_1_out_7), .out_8(decoder38_1_out_8),
    .out_9(decoder38_1_out_9), .out_10(decoder38_1_out_10), .out_11(decoder38_1_out_11));
  not not_1 (not_1_out, in_4);
  and and_1 (out_5, decoder38_1_out_4, not_1_out);
  and and_2 (out_6, decoder38_1_out_5, not_1_out);
  and and_3 (out_7, decoder38_1_out_6, not_1_out);
  and and_4 (out_8, decoder38_1_out_7, not_1_out);
  and and_5 (out_9, decoder38_1_out_8, not_1_out);
  and and_6 (out_10, decoder38_1_out_9, not_1_out);
  and and_7 (out_11, decoder38_1_out_10, not_1_out);
  and and_8 (out_12, decoder38_1_out_11, not_1_out);
  and and_9 (out_13, decoder38_1_out_4, in_4);
  and and_10 (out_14, decoder38_1_out_5, in_4);
  and and_11 (out_15, decoder38_1_out_6, in_4);
  and and_12 (out_16, decoder38_1_out_7, in_4);
  and and_13 (out_17, decoder38_1_out_8, in_4);
  and and_14 (out_18, decoder38_1_out_9, in_4);
  and and_15 (out_19, decoder38_1_out_10, in_4);
  and and_16 (out_20, decoder38_1_out_11, in_4);
endmodule

module encoder164 (
  input  in_1,
  input  in_2,
  input  in_3,
  input  in_4,
  input  in_5,
  input  in_6,
  input  in_7,
  input  in_8,
  input  in_9,
  input  in_10,
  input  in_11,
  input  in_12,
  input  in_13,
  input  in_14,
  input  in_15,
  input  in_16,
  output out_17,
  output out_18,
  output out_19,
  output out_20
);

  wire encoder83_1_out_9, encoder83_1_out_10, encoder83_1_out_11, encoder83_2_out_9, encoder83_2_out_10,
       encoder83_2_out_11;

  encoder83 encoder83_1 (
    .in_1(in_1), .in_2(in_2), .in_3(in_3), .in_4(in_4), .in_5(in_5), .in_6(in_6), .in_7(in_7), .in_8(in_8),
    .out_9(encoder83_1_out_9), .out_10(encoder83_1_out_10), .out_11(encoder83_1_out_11));
  encoder83 encoder83_2 (
    .in_1(in_9), .in_2(in_10), .in_3(in_11), .in_4(in_12), .in_5(in_13), .in_6(in_14), .in_7(in_15),
    .in_8(in_16), .out_9(encoder83_2_out_9), .out_10(encoder83_2_out_10), .out_11(encoder83_2_out_11));
  or or_1 (out_17, encoder83_1_out_9, encoder83_2_out_9);
  or or_2 (out_18, encoder83_1_out_10, encoder83_2_out_10);
  or or_3 (out_19, encoder83_1_out_11, encoder83_2_out_11);
  or or_4 (out_20, in_9, in_10, in_11, in_12, in_13, in_14, in_15, in_16);
endmodule

module prio_encoder42 (
  input  in_1,
  input  in_2,
  input  in_3,
  input  in_4,
  output out_5,
  output out_6
);

  wire and_1_out, not_1_out;

  not not_1 (not_1_out, in_3);
  or or_1 (out_6, in_3, in_4);
  and and_1 (and_1_out, in_2, not_1_out);
  or or_2 (out_5, and_1_out, in_4);
endmodule

module prio_encoder83 (
  input  in_1,
  input  in_2,
  input  in_3,
  input  in_4,
  input  in_5,
  input  in_6,
  input  in_7,
  input  in_8,
  output out_9,
  output out_10,
  output out_11
);

  wire and_1_out, and_2_out, not_1_out, prio_encoder42_1_out_5, prio_encoder42_1_out_6,
       prio_encoder42_2_out_5, prio_encoder42_2_out_6;

  prio_encoder42 prio_encoder42_1 (
    .in_1(in_1), .in_2(in_2), .in_3(in_3), .in_4(in_4), .out_5(prio_encoder42_1_out_5),
    .out_6(prio_encoder42_1_out_6));
  prio_encoder42 prio_encoder42_2 (
    .in_1(in_5), .in_2(in_6), .in_3(in_7), .in_4(in_8), .out_5(prio_encoder42_2_out_5),
    .out_6(prio_encoder42_2_out_6));
  and and_1 (and_1_out, not_1_out, prio_encoder42_1_out_5);
  and and_2 (and_2_out, not_1_out, prio_encoder42_1_out_6);
  not not_1 (not_1_out, out_11);
  or or_1 (out_9, and_1_out, prio_encoder42_2_out_5);
  or or_2 (out_10, and_2_out, prio_encoder42_2_out_6);
  or or_3 (out_11, in_5, in_6, in_7, in_8);
endmodule

module prio_encoder164 (
  input  in_1,
  input  in_2,
  input  in_3,
  input  in_4,
  input  in_5,
  input  in_6,
  input  in_7,
  input  in_8,
  input  in_9,
  input  in_10,
  input  in_11,
  input  in_12,
  input  in_13,
  input  in_14,
  input  in_15,
  input  in_16,
  output out_17,
  output out_18,
  output out_19,
  output out_20
);

  wire and_1_out, and_2_out, and_3_out, not_1_out, prio_encoder83_1_out_9, prio_encoder83_1_out_10,
       prio_encoder83_1_out_11, prio_encoder83_2_out_9, prio_encoder83_2_out_10, prio_encoder83_2_out_11;

  prio_encoder83 prio_encoder83_1 (
    .in_1(in_1), .in_2(in_2), .in_3(in_3), .in_4(in_4), .in_5(in_5), .in_6(in_6), .in_7(in_7), .in_8(in_8),
    .out_9(prio_encoder83_1_out_9), .out_10(prio_encoder83_1_out_10), .out_11(prio_encoder83_1_out_11));
  prio_encoder83 prio_encoder83_2 (
    .in_1(in_9), .in_2(in_10), .in_3(in_11), .in_4(in_12), .in_5(in_13), .in_6(in_14), .in_7(in_15),
    .in_8(in_16), .out_9(prio_encoder83_2_out_9), .out_10(prio_encoder83_2_out_10),
    .out_11(prio_encoder83_2_out_11));
  and and_1 (and_1_out, not_1_out, prio_encoder83_1_out_9);
  and and_2 (and_2_out, not_1_out, prio_encoder83_1_out_10);
  and and_3 (and_3_out, not_1_out, prio_encoder83_1_out_11);
  or or_1 (out_17, and_1_out, prio_encoder83_2_out_9);
  or or_2 (out_18, and_2_out, prio_encoder83_2_out_10);
  or or_3 (out_19, and_3_out, prio_encoder83_2_out_11);
  or or_4 (out_20, in_9, in_10, in_11, in_12, in_13, in_14, in_15, in_16);
  not not_1 (not_1_out, out_20);
endmodule
