// Logisim project vision_instance.circ as structural Verilog
module vision_example (
  input  in_1,
  input  in_2,
  input  in_3,
  input  in_4,
  input  in_5,
  input  in_6,
  input  in_7
);

  _7_Segment_Display u_7_segment_display_1 (
    .g(in_7), .f(in_6), .a(in_1), .b(in_2), .e(in_5), .d(in_4), .c(in_3), .dp(1'b1));
endmodule
