// Logisim project visionable_Subtest4.circ as structural Verilog: 20 circuits, main circuit main
module main (
  input  in_1,
  input  in_2,
  input  in_3,
  input  in_4,
  input  in_5,
  input  in_6,
  input  in_7,
  input  in_8,
  output out_9
);

  wire decoder416_1_out_5, decoder416_1_out_6, decoder416_1_out_7, decoder416_1_out_8, decoder416_1_out_9,
       decoder416_1_out_10, decoder416_1_out_11, decoder416_1_out_12, decoder416_1_out_13,
       decoder416_1_out_14, decoder416_1_out_15, decoder416_1_out_16, decoder416_1_out_17,
       decoder416_1_out_18, decoder416_1_out_19, decoder416_1_out_20, decoder416_2_out_5, decoder416_2_out_6,
       decoder416_2_out_7, decoder416_2_out_8, decoder416_2_out_9, decoder416_2_out_10, decoder416_2_out_11,
       decoder416_2_out_12, decoder416_2_out_13, decoder416_2_out_14, decoder416_2_out_15,
       decoder416_2_out_16, decoder416_2_out_17, decoder416_2_out_18, decoder416_2_out_19,
       decoder416_2_out_20, decoder416_3_out_5, decoder416_3_out_6, decoder416_3_out_7, decoder416_3_out_8,
       decoder416_3_out_9, decoder416_3_out_10, decoder416_3_out_11, decoder416_3_out_12,
       decoder416_3_out_13, decoder416_3_out_14, decoder416_3_out_15, decoder416_3_out_16,
       decoder416_3_out_17, decoder416_3_out_18, decoder416_3_out_19, decoder416_3_out_20,
       segment716_1_out_17, segment716_1_out_18, segment716_1_out_19, segment716_1_out_20,
       segment716_1_out_21, segment716_1_out_22, segment716_1_out_23, segment716_2_out_17,
       segment716_2_out_18, segment716_2_out_19, segment716_2_out_20, segment716_2_out_21,
       segment716_2_out_22, segment716_2_out_23, segment716_3_out_17, segment716_3_out_18,
       segment716_3_out_19, segment716_3_out_20, segment716_3_out_21, segment716_3_out_22,
       segment716_3_out_23, sub4_1_out_9, sub4_1_out_10, sub4_1_out_11, sub4_1_out_12;

  decoder416 decoder416_1 (
    .in_1(in_1), .in_2(in_2), .in_3(in_3), .in_4(in_4), .out_5(decoder416_1_out_5),
    .out_6(decoder416_1_out_6), .out_7(decoder416_1_out_7), .out_8(decoder416_1_out_8),
    .out_9(decoder416_1_out_9), .out_10(decoder416_1_out_10), .out_11(decoder416_1_out_11),
    .out_12(decoder416_1_out_12), .out_13(decoder416_1_out_13), .out_14(decoder416_1_out_14),
    .out_15(decoder416_1_out_15), .out_16(decoder416_1_out_16), .out_17(decoder416_1_out_17),
    .out_18(decoder416_1_out_18), .out_19(decoder416_1_out_19), .out_20(decoder416_1_out_20));
  decoder416 decoder416_2 (
    .in_1(in_5), .in_2(in_6), .in_3(in_7), .in_4(in_8), .out_5(decoder416_2_out_5),
    .out_6(decoder416_2_out_6), .out_7(decoder416_2_out_7), .out_8(decoder416_2_out_8),
    .out_9(decoder416_2_out_9), .out_10(decoder416_2_out_10), .out_11(decoder416_2_out_11),
    .out_12(decoder416_2_out_12), .out_13(decoder416_2_out_13), .out_14(decoder416_2_out_14),
    .out_15(decoder416_2_out_15), .out_16(decoder416_2_out_16), .out_17(decoder416_2_out_17),
    .out_18(decoder416_2_out_18), .out_19(decoder416_2_out_19), .out_20(decoder416_2_out_20));
  sub4 sub4_1 (
    .in_1(in_1), .in_2(in_2), .in_3(in_3), .in_4(in_4), .in_5(in_5), .in_6(in_6), .in_7(in_7), .in_8(in_8),
    .out_9(sub4_1_out_9), .out_10(sub4_1_out_10), .out_11(sub4_1_out_11), .out_12(sub4_1_out_12),
    .out_13(out_9));
  segment716 segment716_1 (
    .in_1(decoder416_1_out_5), .in_2(decoder416_1_out_6), .in_3(decoder416_1_out_7),
    .in_4(decoder416_1_out_8), .in_5(decoder416_1_out_9), .in_6(decoder416_1_out_10),
    .in_7(decoder416_1_out_11), .in_8(decoder416_1_out_12), .in_9(decoder416_1_out_13),
    .in_10(decoder416_1_out_14), .in_11(decoder416_1_out_15), .in_12(decoder416_1_out_16),
    .in_13(decoder416_1_out_17), .in_14(decoder416_1_out_18), .in_15(decoder416_1_out_19),
    .in_16(decoder416_1_out_20), .out_17(segment716_1_out_17), .out_18(segment716_1_out_18),
    .out_19(segment716_1_out_19), .out_20(segment716_1_out_20), .out_21(segment716_1_out_21),
    .out_22(segment716_1_out_22), .out_23(segment716_1_out_23));
  segment716 segment716_2 (
    .in_1(decoder416_2_out_5), .in_2(decoder416_2_out_6), .in_3(decoder416_2_out_7),
    .in_4(decoder416_2_out_8), .in_5(decoder416_2_out_9), .in_6(decoder416_2_out_10),
    .in_7(decoder416_2_out_11), .in_8(decoder416_2_out_12), .in_9(decoder416_2_out_13),
    .in_10(decoder416_2_out_14), .in_11(decoder416_2_out_15), .in_12(decoder416_2_out_16),
    .in_13(decoder416_2_out_17), .in_14(decoder416_2_out_18), .in_15(decoder416_2_out_19),
    .in_16(decoder416_2_out_20), .out_17(segment716_2_out_17), .out_18(segment716_2_out_18),
    .out_19(segment716_2_out_19), .out_20(segment716_2_out_20), .out_21(segment716_2_out_21),
    .out_22(segment716_2_out_22), .out_23(segment716_2_out_23));
  _7_Segment_Display u_7_segment_display_1 (
    .g(segment716_1_out_23), .f(segment716_1_out_22), .a(segment716_1_out_17), .b(segment716_1_out_18),
    .e(segment716_1_out_21), .d(segment716_1_out_20), .c(segment716_1_out_19), .dp(1'b1));
  _7_Segment_Display u_7_segment_display_2 (
    .g(segment716_2_out_23), .f(segment716_2_out_22), .a(segment716_2_out_17), .b(segment716_2_out_18),
    .e(segment716_2_out_21), .d(segment716_2_out_20), .c(segment716_2_out_19), .dp(1'b1));
  decoder416 decoder416_3 (
    .in_1(sub4_1_out_9), .in_2(sub4_1_out_10), .in_3(sub4_1_out_11), .in_4(sub4_1_out_12),
    .out_5(decoder416_3_out_5), .out_6(decoder416_3_out_6), .out_7(decoder416_3_out_7),
    .out_8(decoder416_3_out_8), .out_9(decoder416_3_out_9), .out_10(decoder416_3_out_10),
    .out_11(decoder416_3_out_11), .out_12(decoder416_3_out_12), .out_13(decoder416_3_out_13),
    .out_14(decoder416_3_out_14), .out_15(decoder416_3_out_15), .out_16(decoder416_3_out_16),
    .out_17(decoder416_3_out_17), .out_18(decoder416_3_out_18), .out_19(decoder416_3_out_19),
    .out_20(decoder416_3_out_20));
  _7_Segment_Display u_7_segment_display_3 (
    .g(segment716_3_out_23), .f(segment716_3_out_22), .a(segment716_3_out_17), .b(segment716_3_out_18),
    .e(segment716_3_out_21), .d(segment716_3_out_20), .c(segment716_3_out_19), .dp(1'b1));
  segment716 segment716_3 (
    .in_1(decoder416_3_out_5), .in_2(decoder416_3_out_6), .in_3(decoder416_3_out_7),
    .in_4(decoder416_3_out_8), .in_5(decoder416_3_out_9), .in_6(decoder416_3_out_10),
    .in_7(decoder416_3_out_11), .in_8(decoder416_3_out_12), .in_9(decoder416_3_out_13),
    .in_10(decoder416_3_out_14), .in_11(decoder416_3_out_15), .in_12(decoder416_3_out_16),
    .in_13(decoder416_3_out_17), .in_14(decoder416_3_out_18), .in_15(decoder416_3_out_19),
    .in_16(decoder416_3_out_20), .out_17(segment716_3_out_17), .out_18(segment716_3_out_18),
    .out_19(segment716_3_out_19), .out_20(segment716_3_out_20), .out_21(segment716_3_out_21),
    .out_22(segment716_3_out_22), .out_23(segment716_3_out_23));
endmodule

module encoder42 (
  input  in_1,
  input  in_2,
  input  in_3,
  input  in_4,
  output out_5,
  output out_6
);

  or or_1 (out_5, in_2, in_4);
  or or_2 (out_6, in_3, in_4);
endmodule

module encoder83 (
  input  in_1,
  input  in_2,
  input  in_3,
  input  in_4,
  input  in_5,
  input  in_6,
  input  in_7,
  input  in_8,
  output out_9,
  output out_10,
  output out_11
);

  wire encoder42_1_out_5, encoder42_1_out_6, encoder42_2_out_5, encoder42_2_out_6;

  encoder42 encoder42_1 (
    .in_1(in_1), .in_2(in_2), .in_3(in_3), .in_4(in_4), .out_5(encoder42_1_out_5), .out_6(encoder42_1_out_6));
  encoder42 encoder42_2 (
    .in_1(in_5), .in_2(in_6), .in_3(in_7), .in_4(in_8), .out_5(encoder42_2_out_5), .out_6(encoder42_2_out_6));
  or or_1 (out_9, encoder42_1_out_5, encoder42_2_out_5);
  or or_2 (out_10, encoder42_1_out_6, encoder42_2_out_6);
  or or_3 (out_11, in_5, in_6, in_7, in_8);
endmodule

module decoder12 (
  input  in_1,
  output out_2,
  output out_3
);

  not not_1 (out_2, in_1);

  assign out_3 = in_1;
endmodule

module decoder38 (
  input  in_1,
  input  in_2,
  input  in_3,
  output out_4,
  output out_5,
  output out_6,
  output out_7,
  output out_8,
  output out_9,
  output out_10,
  output out_11
);

  wire and_1_out, and_2_out, and_3_out, and_4_out, not_1_out, not_2_out, not_3_out;

  not not_1 (not_1_out, in_1);
  not not_2 (not_2_out, in_2);
  not not_3 (not_3_out, in_3);
  and and_1 (and_1_out, not_1_out, not_2_out);
  and and_2 (and_2_out, not_1_out, in_2);
  and and_3 (and_3_out, not_2_out, in_1);
  and and_4 (and_4_out, in_1, in_2);
  and and_5 (out_4, and_1_out, not_3_out);
  and and_6 (out_5, and_3_out, not_3_out);
  and and_7 (out_6, and_2_out, not_3_out);
  and and_8 (out_7, and_4_out, not_3_out);
  and and_9 (out_8, and_1_out, in_3);
  and and_10 (out_9, and_3_out, in_3);
  and and_11 (out_10, and_2_out, in_3);
  and and_12 (out_11, and_4_out, in_3);
endmodule

module segment716 (
  input  in_1,
  input  in_2,
  input  in_3,
  input  in_4,
  input  in_5,
  input  in_6,
  input  in_7,
  input  in_8,
  input  in_9,
  input  in_10,
  input  in_11,
  input  in_12,
  input  in_13,
  input  in_14,
  input  in_15,
  input  in_16,
  output out_17,
  output out_18,
  output out_19,
  output out_20,
  output out_21,
  output out_22,
  output out_23
);

  wire segment710_1_out_11, segment710_1_out_12, segment710_1_out_13, segment710_1_out_14,
       segment710_1_out_15, segment710_1_out_16, segment710_1_out_17;

  segment710 segment710_1 (
    .in_1(in_1), .in_2(in_2), .in_3(in_3), .in_4(in_4), .in_5(in_5), .in_6(in_6), .in_7(in_7), .in_8(in_8),
    .in_9(in_9), .in_10(in_10), .out_11(segment710_1_out_11), .out_12(segment710_1_out_12),
    .out_13(segment710_1_out_13), .out_14(segment710_1_out_14), .out_15(segment710_1_out_15),
    .out_16(segment710_1_out_16), .out_17(segment710_1_out_17));
  or or_1 (out_17, segment710_1_out_11, in_11, in_13, in_15, in_16);
  or or_2 (out_18, segment710_1_out_12, in_11, in_14);
  or or_3 (out_19, in_11, segment710_1_out_13, in_12, in_14);
  or or_4 (out_20, in_12, segment710_1_out_14, in_13, in_14, in_15);
  or or_5 (out_21, in_16, in_13, segment710_1_out_15, in_11, in_14, in_12, in_15);
  or or_6 (out_22, in_13, segment710_1_out_16, in_11, in_12, in_15, in_16);
  or or_7 (out_23, segment710_1_out_17, in_11, in_12, in_14, in_15, in_16);
endmodule

module segment710 (
  input  in_1,
  input  in_2,
  input  in_3,
  input  in_4,
  input  in_5,
  input  in_6,
  input  in_7,
  input  in_8,
  input  in_9,
  input  in_10,
  output out_11,
  output out_12,
  output out_13,
  output out_14,
  output out_15,
  output out_16,
  output out_17
);

  or or_1 (out_11, in_1, in_3, in_4, in_6, in_7, in_8, in_9, in_10);
  or or_2 (out_12, in_1, in_3, in_4, in_5, in_8, in_9, in_10, in_2);
  or or_3 (out_13, in_1, in_2, in_4, in_5, in_6, in_7, in_8, in_9, in_10);
  or or_4 (out_14, in_1, in_3, in_4, in_6, in_7, in_9, in_10);
  or or_5 (out_15, in_1, in_3, in_7, in_9);
  or or_6 (out_16, in_1, in_5, in_6, in_7, in_9, in_10);
  or or_7 (out_17, in_3, in_4, in_5, in_6, in_7, in_9, in_10);
endmodule

module decoder416 (
  input  in_1,
  input  in_2,
  input  in_3,
  input  in_4,
  output out_5,
  output out_6,
  output out_7,
  output out_8,
  output out_9,
  output out_10,
  output out_11,
  output out_12,
  output out_13,
  output out_14,
  output out_15,
  output out_16,
  output out_17,
  output out_18,
  output out_19,
  output out_20
);

  wire decoder38_1_out_4, decoder38_1_out_5, decoder38_1_out_6, decoder38_1_out_7, decoder38_1_out_8,
       decoder38_1_out_9, decoder38_1_out_10, decoder38_1_out_11, not_1_out;

  decoder38 decoder38_1 (
    .in_1(in_1), .in_2(in_2), .in_3(in_3), .out_4(decoder38_1_out_4), .out_5(decoder38_1_out_5),
    .out_6(decoder38_1_out_6), .out_7(decoder38_1_out_7), .out_8(decoder38_1_out_8),
    .out_9(decoder38_1_out_9), .out_10(decoder38_1_out_10), .out_11(decoder38_1_out_11));
  not not_1 (not_1_out, in_4);
  and and_1 (out_5, decoder38_1_out_4, not_1_out);
  and and_2 (out_6, decoder38_1_out_5, not_1_out);
  and and_3 (out_7, decoder38_1_out_6, not_1_out);
  and and_4 (out_8, decoder38_1_out_7, not_1_out);
  and and_5 (out_9, decoder38_1_out_8, not_1_out);
  and and_6 (out_10, decoder38_1_out_9, not_1_out);
  and and_7 (out_11, decoder38_1_out_10, not_1_out);
  and and_8 (out_12, decoder38_1_out_11, not_1_out);
  and and_9 (out_13, decoder38_1_out_4, in_4);
  and and_10 (out_14, decoder38_1_out_5, in_4);
  and and_11 (out_15, decoder38_1_out_6, in_4);
  and and_12 (out_16, decoder38_1_out_7, in_4);
  and and_13 (out_17, decoder38_1_out_8, in_4);
  and and_14 (out_18, decoder38_1_out_9, in_4);
  and and_15 (out_19, decoder38_1_out_10, in_4);
  and and_16 (out_20, decoder38_1_out_11, in_4);
endmodule

module encoder164 (
  input  in_1,
  input  in_2,
  input  in_3,
  input  in_4,
  input  in_5,
  input  in_6,
  input  in_7,
  input  in_8,
  input  in_9,
  input  in_10,
  input  in_11,
  input  in_12,
  input  in_13,
  input  in_14,
  input  in_15,
  input  in_16,
  output out_17,
  output out_18,
  output out_19,
  output out_20
);

  wire encoder83_1_out_9, encoder83_1_out_10, encoder83_1_out_11, encoder83_2_out_9, encoder83_2_out_10,
       encoder83_2_out_11;

  encoder83 encoder83_1 (
    .in_1(in_1), .in_2(in_2), .in_3(in_3), .in_4(in_4), .in_5(in_5), .in_6(in_6), .in_7(in_7), .in_8(in_8),
    .out_9(encoder83_1_out_9), .out_10(encoder83_1_out_10), .out_11(encoder83_1_out_11));
  encoder83 encoder83_2 (
    .in_1(in_9), .in_2(in_10), .in_3(in_11), .in_4(in_12), .in_5(in_13), .in_6(in_14), .in_7(in_15),
    .in_8(in_16), .out_9(encoder83_2_out_9), .out_10(encoder83_2_out_10), .out_11(encoder83_2_out_11));
  or or_1 (out_17, encoder83_1_out_9, encoder83_2_out_9);
  or or_2 (out_18, encoder83_1_out_10, encoder83_2_out_10);
  or or_3 (out_19, encoder83_1_out_11, encoder83_2_out_11);
  or or_4 (out_20, in_9, in_10, in_11, in_12, in_13, in_14, in_15, in_16);
endmodule

module prio_encoder42 (
  input  in_1,
  input  in_2,
  input  in_3,
  input  in_4,
  output out_5,
  output out_6
);

  wire and_1_out, not_1_out;

  not not_1 (not_1_out, in_3);
  or or_1 (out_6, in_3, in_4);
  and and_1 (and_1_out, in_2, not_1_out);
  or or_2 (out_5, and_1_out, in_4);
endmodule

module prio_encoder83 (
  input  in_1,
  input  in_2,
  input  in_3,
  input  in_4,
  input  in_5,
  input  in_6,
  input  in_7,
  input  in_8,
  output out_9,
  output out_10,
  output out_11
);

  wire and_1_out, and_2_out, not_1_out, prio_encoder42_1_out_5, prio_encoder42_1_out_6,
       prio_encoder42_2_out_5, prio_encoder42_2_out_6;

  prio_encoder42 prio_encoder42_1 (
    .in_1(in_1), .in_2(in_2), .in_3(in_3), .in_4(in_4), .out_5(prio_encoder42_1_out_5),
    .out_6(prio_encoder42_1_out_6));
  prio_encoder42 prio_encoder42_2 (
    .in_1(in_5), .in_2(in_6), .in_3(in_7), .in_4(in_8), .out_5(prio_encoder42_2_out_5),
    .out_6(prio_encoder42_2_out_6));
  and and_1 (and_1_out, not_1_out, prio_encoder42_1_out_5);
  and and_2 (and_2_out, not_1_out, prio_encoder42_1_out_6);
  not not_1 (not_1_out, out_11);
  or or_1 (out_9, and_1_out, prio_encoder42_2_out_5);
  or or_2 (out_10, and_2_out, prio_encoder42_2_out_6);
  or or_3 (out_11, in_5, in_6, in_7, in_8);
endmodule

module prio_encoder164 (
  input  in_1,
  input  in_2,
  input  in_3,
  input  in_4,
  input  in_5,
  input  in_6,
  input  in_7,
  input  in_8,
  input  in_9,
  input  in_10,
  input  in_11,
  input  in_12,
  input  in_13,
  input  in_14,
  input  in_15,
  input  in_16,
  output out_17,
  output out_18,
  output out_19,
  output out_20
);

  wire and_1_out, and_2_out, and_3_out, not_1_out, prio_encoder83_1_out_9, prio_encoder83_1_out_10,
       prio_encoder83_1_out_11, prio_encoder83_2_out_9, prio_encoder83_2_out_10, prio_encoder83_2_out_11;

  prio_encoder83 prio_encoder83_1 (
    .in_1(in_1), .in_2(in_2), .in_3(in_3), .in_4(in_4), .in_5(in_5), .in_6(in_6), .in_7(in_7), .in_8(in_8),
    .out_9(prio_encoder83_1_out_9), .out_10(prio_encoder83_1_out_10), .out_11(prio_encoder83_1_out_11));
  prio_encoder83 prio_encoder83_2 (
    .in_1(in_9), .in_2(in_10), .in_3(in_11), .in_4(in_12), .in_5(in_13), .in_6(in_14), .in_7(in_15),
    .in_8(in_16), .out_9(prio_encoder83_2_out_9), .out_10(prio_encoder83_2_out_10),
    .out_11(prio_encoder83_2_out_11));
  and and_1 (and_1_out, not_1_out, prio_encoder83_1_out_9);
  and and_2 (and_2_out, not_1_out, prio_encoder83_1_out_10);
  and and_3 (and_3_out, not_1_out, prio_encoder83_1_out_11);
  or or_1 (out_17, and_1_out, prio_encoder83_2_out_9);
  or or_2 (out_18, and_2_out, prio_encoder83_2_out_10);
  or or_3 (out_19, and_3_out, prio_encoder83_2_out_11);
  or or_4 (out_20, in_9, in_10, in_11, in_12, in_13, in_14, in_15, in_16);
  not not_1 (not_1_out, out_20);
endmodule

module comparator4 (
  input  in_1,
  input  in_2,
  input  in_3,
  input  in_4,
  input  in_5,
  input  in_6,
  input  in_7,
  input  in_8,
  output out_9
);

  wire xor_1_out, xor_2_out, xor_3_out, xor_4_out;

  xor xor_1 (xor_1_out, in_1, in_2);
  xor xor_2 (xor_2_out, in_3, in_4);
  xor xor_3 (xor_3_out, in_5, in_6);
  xor xor_4 (xor_4_out, in_7, in_8);
  nor nor_1 (out_9, xor_2_out, xor_3_out, xor_4_out);
endmodule

module add1 (
  input  in_1,
  input  in_2,
  input  in_3,
  output out_4,
  output out_5
);

  wire and_1_out, and_2_out, and_3_out, xor_1_out;

  and and_1 (and_1_out, in_2, in_1);
  and and_2 (and_2_out, in_3, in_1);
  and and_3 (and_3_out, in_2, in_3);
  xor xor_1 (xor_1_out, in_2, in_1);
  xor xor_2 (out_4, xor_1_out, in_3);
  or or_1 (out_5, and_1_out, and_2_out, and_3_out);
endmodule

module Half_add1 (
  input  in_1,
  input  in_2,
  output out_3,
  output out_4
);

  xor xor_1 (out_3, in_1, in_2);
  and and_1 (out_4, in_1, in_2);
endmodule

module Halfull_add1 (
  input  in_1,
  input  in_2,
  input  in_3,
  output out_4,
  output out_5
);

  wire half_add1_1_out_3, half_add1_1_out_4, half_add1_2_out_4;

  Half_add1 half_add1_1 (.in_1(in_2), .in_2(in_3), .out_3(half_add1_1_out_3), .out_4(half_add1_1_out_4));
  Half_add1 half_add1_2 (.in_1(in_1), .in_2(half_add1_1_out_3), .out_3(out_4), .out_4(half_add1_2_out_4));
  Half_add1 half_add1_3 (.in_1(half_add1_2_out_4), .in_2(half_add1_1_out_4), .out_3(out_5));  // open: out_4
endmodule

module add4 (
  input  in_1,
  input  in_2,
  input  in_3,
  input  in_4,
  input  in_5,
  input  in_6,
  input  in_7,
  input  in_8,
  output out_9,
  output out_10,
  output out_11,
  output out_12,
  output out_13
);

  wire halfull_add1_1_out_5, halfull_add1_2_out_5, halfull_add1_3_out_5;

  Halfull_add1 halfull_add1_1 (.in_2(in_1), .in_3(in_5), .out_4(out_9), .out_5(halfull_add1_1_out_5));  // open: in_1
  Halfull_add1 halfull_add1_2 (
    .in_1(halfull_add1_1_out_5), .in_2(in_2), .in_3(in_6), .out_4(out_10), .out_5(halfull_add1_2_out_5));
  Halfull_add1 halfull_add1_3 (
    .in_1(halfull_add1_2_out_5), .in_2(in_3), .in_3(in_7), .out_4(out_11), .out_5(halfull_add1_3_out_5));
  Halfull_add1 halfull_add1_4 (.in_1(halfull_add1_3_out_5), .in_2(in_4), .in_3(in_8), .out_4(out_12), .out_5(out_13));
endmodule

module vision_example (
  input  in_1,
  input  in_2,
  input  in_3,
  input  in_4,
  input  in_5,
  input  in_6,
  input  in_7
);

  _7_Segment_Display u_7_segment_display_1 (
    .g(in_7), .f(in_6), .a(in_1), .b(in_2), .e(in_5), .d(in_4), .c(in_3), .dp(1'b1));
endmodule

module sub4 (
  input  in_1,
  input  in_2,
  input  in_3,
  input  in_4,
  input  in_5,
  input  in_6,
  input  in_7,
  input  in_8,
  output out_9,
  output out_10,
  output out_11,
  output out_12,
  output out_13
);

  wire add4_1_out_9, add4_1_out_10, add4_1_out_11, add4_1_out_12, add4_1_out_13, add4_2_out_13, not_1_out,
       not_2_out, not_3_out, not_4_out, not_5_out, not_6_out;

  not not_1 (not_1_out, in_5);
  not not_2 (not_2_out, in_6);
  not not_3 (not_3_out, in_7);
  not not_4 (not_4_out, in_8);
  add4 add4_1 (
    .in_1(1'b1), .in_5(not_1_out), .in_6(not_2_out), .in_7(not_3_out), .in_8(not_4_out),
    .out_9(add4_1_out_9), .out_10(add4_1_out_10), .out_11(add4_1_out_11), .out_12(add4_1_out_12),
    .out_13(add4_1_out_13));  // open: in_2, in_3, in_4
  add4 add4_2 (
    .in_1(in_1), .in_2(in_2), .in_3(in_3), .in_4(in_4), .in_5(add4_1_out_9), .in_6(add4_1_out_10),
    .in_7(add4_1_out_11), .in_8(add4_1_out_12), .out_9(out_9), .out_10(out_10), .out_11(out_11),
    .out_12(out_12), .out_13(add4_2_out_13));
  not not_5 (not_5_out, add4_2_out_13);
  not not_6 (not_6_out, add4_1_out_13);
  and and_1 (out_13, not_5_out, not_6_out);
endmodule

module Self_XOR (
  input  in_1,
  input  in_2,
  input  in_3,
  input  in_4,
  input  in_5,
  input  in_6,
  output out_7,
  output out_8,
  output out_9
);

  wire and_1_out, and_2_out, and_3_out, and_4_out, nand_1_out, nand_2_out, not_1_out, not_2_out, or_1_out;

  not not_1 (not_1_out, in_6);
  not not_2 (not_2_out, in_5);
  or or_1 (or_1_out, in_2, in_1);
  nand nand_1 (nand_1_out, in_3, in_4);
  and and_1 (and_1_out, in_5, not_1_out);
  and and_2 (and_2_out, not_2_out, in_6);
  nand nand_2 (nand_2_out, in_1, in_2);
  and and_3 (and_3_out, in_3, nand_1_out);
  and and_4 (and_4_out, nand_1_out, in_4);
  or or_2 (out_9, and_1_out, and_2_out);
  and and_5 (out_7, or_1_out, nand_2_out);
  or or_3 (out_8, and_3_out, and_4_out);
endmodule
