// Logisim project sCPU.circ as structural Verilog: 30 circuits, main circuit main
module main (
  input  [7:0] in_1,
  output [7:0] out_2
);

  wire clock_1_out, decoder_1_out0, decoder_1_out1, decoder_1_out2, decoder_1_out3, decoder_2_out0,
       decoder_3_out0, decoder_4_out0, or_1_out, transmission_1_p2, transmission_2_p2, transmission_3_p2,
       transmission_4_p2;
  wire [7:0] adder_1_out, register_5_q, transmission_1_p4, transmission_2_p4;
  wire [7:6] transmission_1_p1;

  Decoder #(.select(2)) decoder_1 (
    .out0(decoder_1_out0), .out1(decoder_1_out1), .out2(decoder_1_out2), .out3(decoder_1_out3),
    .sel(in_1[7:6]));  // open: en
  // Transmission_Gate #(.width(8)) transmission_1: pin names not known; wires that end beside it: {transmission_1_p1, in_1[5:0]}, transmission_1_p2, decoder_1_out0, transmission_1_p4
  not not_1 (transmission_1_p2, decoder_1_out0);
  Decoder #(.select(2)) decoder_2 (.out0(decoder_2_out0), .sel(transmission_1_p4[1:0]));  // open: out1, out2, out3, en
  Decoder #(.select(2)) decoder_3 (.out0(decoder_3_out0), .sel(transmission_1_p4[3:2]));  // open: out1, out2, out3, en
  Decoder #(.select(2)) decoder_4 (.out0(decoder_4_out0), .sel(transmission_1_p4[5:4]));  // open: out1, out2, out3, en
  // Transmission_Gate #(.width(8)) transmission_2: pin names not known; wires that end beside it: {transmission_1_p1, in_1[5:0]}, transmission_2_p2, decoder_1_out2, transmission_2_p4
  not not_2 (transmission_2_p2, decoder_1_out2);
  PLA pla_1 ();  // open: in, out
  or or_1 (or_1_out, decoder_2_out0, decoder_3_out0, decoder_4_out0, decoder_1_out2);
  // Transmission_Gate #(.width(8)) transmission_3: pin names not known; wires that end beside it: {transmission_1_p1, in_1[5:0]}, transmission_3_p2, decoder_1_out1
  not not_3 (transmission_3_p2, decoder_1_out1);
  // Transmission_Gate #(.width(8)) transmission_4: pin names not known; wires that end beside it: {transmission_1_p1, in_1[5:0]}, transmission_4_p2, decoder_1_out3
  not not_4 (transmission_4_p2, decoder_1_out3);
  Clock clock_1 (.out(clock_1_out));
  Register register_1 (.D(transmission_2_p4), .en(or_1_out), .clk(clock_1_out));  // open: Q, clr
  Register register_2 (.clk(clock_1_out));  // open: D, en, Q, clr
  Register register_3 (.clk(clock_1_out));  // open: D, en, Q, clr
  Register register_4 (.clk(clock_1_out));  // open: D, en, Q, clr
  Register register_5 (.D(adder_1_out), .en(1'b1), .clk(clock_1_out), .Q(register_5_q));  // open: clr
  Adder adder_1 (.a(register_5_q), .b(8'h1), .out(adder_1_out));  // open: cin, cout
endmodule

module SR_Latch (
  input  in_1,
  input  in_2,
  output out_3,
  output out_4
);

  nor nor_1 (out_3, in_1, out_4);
  nor nor_2 (out_4, out_3, in_2);
endmodule

module D_Latch (
  input  in_1,
  input  in_2,
  input  in_3,
  output out_4,
  output out_5
);

  wire and_1_out, and_2_out, and_3_out, not_1_out, not_2_out, or_1_out;

  not not_1 (not_1_out, in_3);
  and and_1 (and_1_out, in_1, not_1_out);
  or or_1 (or_1_out, in_2, in_3);
  and and_2 (and_2_out, and_1_out, or_1_out);
  and and_3 (and_3_out, or_1_out, not_2_out);
  not not_2 (not_2_out, and_1_out);
  SR_Latch sr_latch_1 (.in_1(and_2_out), .in_2(and_3_out), .out_3(out_5), .out_4(out_4));
  // AND_Gate and_4 is placed but not wired
endmodule

module NSR_Latch (
  input  in_1,
  input  in_2,
  output out_3,
  output out_4
);

  nand nand_1 (out_3, in_1, out_4);
  nand nand_2 (out_4, out_3, in_2);
endmodule

module ND_Latch (
  input  in_1,
  input  in_2,
  output out_3,
  output out_4
);

  wire and_1_out, and_2_out, not_1_out;

  not not_1 (not_1_out, in_2);
  and and_1 (and_1_out, in_2, in_1);
  and and_2 (and_2_out, in_1, not_1_out);
  NSR_Latch nsr_latch_1 (.in_1(and_1_out), .in_2(and_2_out), .out_3(out_3), .out_4(out_4));
endmodule

module D_flipflop (
  input  in_1,
  input  in_2,
  input  in_3,
  input  in_4,
  output out_5,
  output out_6
);

  wire and_1_out, d_latch_1_out_4, not_1_out;

  and and_1 (and_1_out, in_1, in_2);
  not not_1 (not_1_out, in_3);
  D_Latch d_latch_1 (.in_1(and_1_out), .in_2(not_1_out), .in_3(in_4), .out_4(d_latch_1_out_4));  // open: out_5
  D_Latch d_latch_2 (.in_1(d_latch_1_out_4), .in_2(in_3), .in_3(in_4), .out_4(out_5), .out_5(out_6));
endmodule

module encoder42 (
  input  in_1,
  input  in_2,
  input  in_3,
  input  in_4,
  output out_5,
  output out_6
);

  or or_1 (out_5, in_2, in_4);
  or or_2 (out_6, in_3, in_4);
endmodule

module encoder83 (
  input  in_1,
  input  in_2,
  input  in_3,
  input  in_4,
  input  in_5,
  input  in_6,
  input  in_7,
  input  in_8,
  output out_9,
  output out_10,
  output out_11
);

  wire encoder42_1_out_5, encoder42_1_out_6, encoder42_2_out_5, encoder42_2_out_6;

  encoder42 encoder42_1 (
    .in_1(in_1), .in_2(in_2), .in_3(in_3), .in_4(in_4), .out_5(encoder42_1_out_5), .out_6(encoder42_1_out_6));
  encoder42 encoder42_2 (
    .in_1(in_5), .in_2(in_6), .in_3(in_7), .in_4(in_8), .out_5(encoder42_2_out_5), .out_6(encoder42_2_out_6));
  or or_1 (out_9, encoder42_1_out_5, encoder42_2_out_5);
  or or_2 (out_10, encoder42_1_out_6, encoder42_2_out_6);
  or or_3 (out_11, in_5, in_6, in_7, in_8);
endmodule

module decoder12 (
  input  in_1,
  output out_2,
  output out_3
);

  not not_1 (out_2, in_1);

  assign out_3 = in_1;
endmodule

module decoder38 (
  input  in_1,
  input  in_2,
  input  in_3,
  output out_4,
  output out_5,
  output out_6,
  output out_7,
  output out_8,
  output out_9,
  output out_10,
  output out_11
);

  wire and_1_out, and_2_out, and_3_out, and_4_out, not_1_out, not_2_out, not_3_out;

  not not_1 (not_1_out, in_1);
  not not_2 (not_2_out, in_2);
  not not_3 (not_3_out, in_3);
  and and_1 (and_1_out, not_1_out, not_2_out);
  and and_2 (and_2_out, not_1_out, in_2);
  and and_3 (and_3_out, not_2_out, in_1);
  and and_4 (and_4_out, in_1, in_2);
  and and_5 (out_4, and_1_out, not_3_out);
  and and_6 (out_5, and_3_out, not_3_out);
  and and_7 (out_6, and_2_out, not_3_out);
  and and_8 (out_7, and_4_out, not_3_out);
  and and_9 (out_8, and_1_out, in_3);
  and and_10 (out_9, and_3_out, in_3);
  and and_11 (out_10, and_2_out, in_3);
  and and_12 (out_11, and_4_out, in_3);
endmodule

module segment716 (
  input  in_1,
  input  in_2,
  input  in_3,
  input  in_4,
  input  in_5,
  input  in_6,
  input  in_7,
  input  in_8,
  input  in_9,
  input  in_10,
  input  in_11,
  input  in_12,
  input  in_13,
  input  in_14,
  input  in_15,
  input  in_16,
  output out_17,
  output out_18,
  output out_19,
  output out_20,
  output out_21,
  output out_22,
  output out_23
);

  wire segment710_1_out_11, segment710_1_out_12, segment710_1_out_13, segment710_1_out_14,
       segment710_1_out_15, segment710_1_out_16, segment710_1_out_17;

  segment710 segment710_1 (
    .in_1(in_1), .in_2(in_2), .in_3(in_3), .in_4(in_4), .in_5(in_5), .in_6(in_6), .in_7(in_7), .in_8(in_8),
    .in_9(in_9), .in_10(in_10), .out_11(segment710_1_out_11), .out_12(segment710_1_out_12),
    .out_13(segment710_1_out_13), .out_14(segment710_1_out_14), .out_15(segment710_1_out_15),
    .out_16(segment710_1_out_16), .out_17(segment710_1_out_17));
  or or_1 (out_17, segment710_1_out_11, in_11, in_13, in_15, in_16);
  or or_2 (out_18, segment710_1_out_12, in_11, in_14);
  or or_3 (out_19, in_11, segment710_1_out_13, in_12, in_14);
  or or_4 (out_20, in_12, segment710_1_out_14, in_13, in_14, in_15);
  or or_5 (out_21, in_16, in_13, segment710_1_out_15, in_11, in_14, in_12, in_15);
  or or_6 (out_22, in_13, segment710_1_out_16, in_11, in_12, in_15, in_16);
  or or_7 (out_23, segment710_1_out_17, in_11, in_12, in_14, in_15, in_16);
endmodule

module segment710 (
  input  in_1,
  input  in_2,
  input  in_3,
  input  in_4,
  input  in_5,
  input  in_6,
  input  in_7,
  input  in_8,
  input  in_9,
  input  in_10,
  output out_11,
  output out_12,
  output out_13,
  output out_14,
  output out_15,
  output out_16,
  output out_17
);

  or or_1 (out_11, in_1, in_3, in_4, in_6, in_7, in_8, in_9, in_10);
  or or_2 (out_12, in_1, in_3, in_4, in_5, in_8, in_9, in_10, in_2);
  or or_3 (out_13, in_1, in_2, in_4, in_5, in_6, in_7, in_8, in_9, in_10);
  or or_4 (out_14, in_1, in_3, in_4, in_6, in_7, in_9, in_10);
  or or_5 (out_15, in_1, in_3, in_7, in_9);
  or or_6 (out_16, in_1, in_5, in_6, in_7, in_9, in_10);
  or or_7 (out_17, in_3, in_4, in_5, in_6, in_7, in_9, in_10);
endmodule

module decoder416 (
  input  in_1,
  input  in_2,
  input  in_3,
  input  in_4,
  output out_5,
  output out_6,
  output out_7,
  output out_8,
  output out_9,
  output out_10,
  output out_11,
  output out_12,
  output out_13,
  output out_14,
  output out_15,
  output out_16,
  output out_17,
  output out_18,
  output out_19,
  output out_20
);

  wire decoder38_1_out_4, decoder38_1_out_5, decoder38_1_out_6, decoder38_1_out_7, decoder38_1_out_8,
       decoder38_1_out_9, decoder38_1_out_10, decoder38_1_out_11, not_1_out;

  decoder38 decoder38_1 (
    .in_1(in_1), .in_2(in_2), .in_3(in_3), .out_4(decoder38_1_out_4), .out_5(decoder38_1_out_5),
    .out_6(decoder38_1_out_6), .out_7(decoder38_1_out_7), .out_8(decoder38_1_out_8),
    .out_9(decoder38_1_out_9), .out_10(decoder38_1_out_10), .out_11(decoder38_1_out_11));
  not not_1 (not_1_out, in_4);
  and and_1 (out_5, decoder38_1_out_4, not_1_out);
  and and_2 (out_6, decoder38_1_out_5, not_1_out);
  and and_3 (out_7, decoder38_1_out_6, not_1_out);
  and and_4 (out_8, decoder38_1_out_7, not_1_out);
  and and_5 (out_9, decoder38_1_out_8, not_1_out);
  and and_6 (out_10, decoder38_1_out_9, not_1_out);
  and and_7 (out_11, decoder38_1_out_10, not_1_out);
  and and_8 (out_12, decoder38_1_out_11, not_1_out);
  and and_9 (out_13, decoder38_1_out_4, in_4);
  and and_10 (out_14, decoder38_1_out_5, in_4);
  and and_11 (out_15, decoder38_1_out_6, in_4);
  and and_12 (out_16, decoder38_1_out_7, in_4);
  and and_13 (out_17, decoder38_1_out_8, in_4);
  and and_14 (out_18, decoder38_1_out_9, in_4);
  and and_15 (out_19, decoder38_1_out_10, in_4);
  and and_16 (out_20, decoder38_1_out_11, in_4);
endmodule

module encoder164 (
  input  in_1,
  input  in_2,
  input  in_3,
  input  in_4,
  input  in_5,
  input  in_6,
  input  in_7,
  input  in_8,
  input  in_9,
  input  in_10,
  input  in_11,
  input  in_12,
  input  in_13,
  input  in_14,
  input  in_15,
  input  in_16,
  output out_17,
  output out_18,
  output out_19,
  output out_20
);

  wire encoder83_1_out_9, encoder83_1_out_10, encoder83_1_out_11, encoder83_2_out_9, encoder83_2_out_10,
       encoder83_2_out_11;

  encoder83 encoder83_1 (
    .in_1(in_1), .in_2(in_2), .in_3(in_3), .in_4(in_4), .in_5(in_5), .in_6(in_6), .in_7(in_7), .in_8(in_8),
    .out_9(encoder83_1_out_9), .out_10(encoder83_1_out_10), .out_11(encoder83_1_out_11));
  encoder83 encoder83_2 (
    .in_1(in_9), .in_2(in_10), .in_3(in_11), .in_4(in_12), .in_5(in_13), .in_6(in_14), .in_7(in_15),
    .in_8(in_16), .out_9(encoder83_2_out_9), .out_10(encoder83_2_out_10), .out_11(encoder83_2_out_11));
  or or_1 (out_17, encoder83_1_out_9, encoder83_2_out_9);
  or or_2 (out_18, encoder83_1_out_10, encoder83_2_out_10);
  or or_3 (out_19, encoder83_1_out_11, encoder83_2_out_11);
  or or_4 (out_20, in_9, in_10, in_11, in_12, in_13, in_14, in_15, in_16);
endmodule

module prio_encoder42 (
  input  in_1,
  input  in_2,
  input  in_3,
  input  in_4,
  output out_5,
  output out_6
);

  wire and_1_out, not_1_out;

  not not_1 (not_1_out, in_3);
  or or_1 (out_6, in_3, in_4);
  and and_1 (and_1_out, in_2, not_1_out);
  or or_2 (out_5, and_1_out, in_4);
endmodule

module prio_encoder83 (
  input  in_1,
  input  in_2,
  input  in_3,
  input  in_4,
  input  in_5,
  input  in_6,
  input  in_7,
  input  in_8,
  output out_9,
  output out_10,
  output out_11
);

  wire and_1_out, and_2_out, not_1_out, prio_encoder42_1_out_5, prio_encoder42_1_out_6,
       prio_encoder42_2_out_5, prio_encoder42_2_out_6;

  prio_encoder42 prio_encoder42_1 (
    .in_1(in_1), .in_2(in_2), .in_3(in_3), .in_4(in_4), .out_5(prio_encoder42_1_out_5),
    .out_6(prio_encoder42_1_out_6));
  prio_encoder42 prio_encoder42_2 (
    .in_1(in_5), .in_2(in_6), .in_3(in_7), .in_4(in_8), .out_5(prio_encoder42_2_out_5),
    .out_6(prio_encoder42_2_out_6));
  and and_1 (and_1_out, not_1_out, prio_encoder42_1_out_5);
  and and_2 (and_2_out, not_1_out, prio_encoder42_1_out_6);
  not not_1 (not_1_out, out_11);
  or or_1 (out_9, and_1_out, prio_encoder42_2_out_5);
  or or_2 (out_10, and_2_out, prio_encoder42_2_out_6);
  or or_3 (out_11, in_5, in_6, in_7, in_8);
endmodule

module prio_encoder164 (
  input  in_1,
  input  in_2,
  input  in_3,
  input  in_4,
  input  in_5,
  input  in_6,
  input  in_7,
  input  in_8,
  input  in_9,
  input  in_10,
  input  in_11,
  input  in_12,
  input  in_13,
  input  in_14,
  input  in_15,
  input  in_16,
  output out_17,
  output out_18,
  output out_19,
  output out_20
);

  wire and_1_out, and_2_out, and_3_out, not_1_out, prio_encoder83_1_out_9, prio_encoder83_1_out_10,
       prio_encoder83_1_out_11, prio_encoder83_2_out_9, prio_encoder83_2_out_10, prio_encoder83_2_out_11;

  prio_encoder83 prio_encoder83_1 (
    .in_1(in_1), .in_2(in_2), .in_3(in_3), .in_4(in_4), .in_5(in_5), .in_6(in_6), .in_7(in_7), .in_8(in_8),
    .out_9(prio_encoder83_1_out_9), .out_10(prio_encoder83_1_out_10), .out_11(prio_encoder83_1_out_11));
  prio_encoder83 prio_encoder83_2 (
    .in_1(in_9), .in_2(in_10), .in_3(in_11), .in_4(in_12), .in_5(in_13), .in_6(in_14), .in_7(in_15),
    .in_8(in_16), .out_9(prio_encoder83_2_out_9), .out_10(prio_encoder83_2_out_10),
    .out_11(prio_encoder83_2_out_11));
  and and_1 (and_1_out, not_1_out, prio_encoder83_1_out_9);
  and and_2 (and_2_out, not_1_out, prio_encoder83_1_out_10);
  and and_3 (and_3_out, not_1_out, prio_encoder83_1_out_11);
  or or_1 (out_17, and_1_out, prio_encoder83_2_out_9);
  or or_2 (out_18, and_2_out, prio_encoder83_2_out_10);
  or or_3 (out_19, and_3_out, prio_encoder83_2_out_11);
  or or_4 (out_20, in_9, in_10, in_11, in_12, in_13, in_14, in_15, in_16);
  not not_1 (not_1_out, out_20);
endmodule

module comparator4 (
  input  in_1,
  input  in_2,
  input  in_3,
  input  in_4,
  input  in_5,
  input  in_6,
  input  in_7,
  input  in_8,
  output out_9
);

  wire xor_1_out, xor_2_out, xor_3_out, xor_4_out;

  xor xor_1 (xor_1_out, in_1, in_2);
  xor xor_2 (xor_2_out, in_3, in_4);
  xor xor_3 (xor_3_out, in_5, in_6);
  xor xor_4 (xor_4_out, in_7, in_8);
  nor nor_1 (out_9, xor_2_out, xor_3_out, xor_4_out);
endmodule

module add1 (
  input  in_1,
  input  in_2,
  input  in_3,
  output out_4,
  output out_5
);

  wire and_1_out, and_2_out, and_3_out, xor_1_out;

  and and_1 (and_1_out, in_2, in_1);
  and and_2 (and_2_out, in_3, in_1);
  and and_3 (and_3_out, in_2, in_3);
  xor xor_1 (xor_1_out, in_2, in_1);
  xor xor_2 (out_4, xor_1_out, in_3);
  or or_1 (out_5, and_1_out, and_2_out, and_3_out);
endmodule

module Half_add1 (
  input  in_1,
  input  in_2,
  output out_3,
  output out_4
);

  xor xor_1 (out_3, in_1, in_2);
  and and_1 (out_4, in_1, in_2);
endmodule

module Halfull_add1 (
  input  in_1,
  input  in_2,
  input  in_3,
  output out_4,
  output out_5
);

  wire half_add1_1_out_3, half_add1_1_out_4, half_add1_2_out_4;

  Half_add1 half_add1_1 (.in_1(in_2), .in_2(in_3), .out_3(half_add1_1_out_3), .out_4(half_add1_1_out_4));
  Half_add1 half_add1_2 (.in_1(in_1), .in_2(half_add1_1_out_3), .out_3(out_4), .out_4(half_add1_2_out_4));
  Half_add1 half_add1_3 (.in_1(half_add1_2_out_4), .in_2(half_add1_1_out_4), .out_3(out_5));  // open: out_4
endmodule

module add4 (
  input  in_1,
  input  in_2,
  input  in_3,
  input  in_4,
  input  in_5,
  input  in_6,
  input  in_7,
  input  in_8,
  output out_9,
  output out_10,
  output out_11,
  output out_12,
  output out_13
);

  wire halfull_add1_1_out_5, halfull_add1_2_out_5, halfull_add1_3_out_5;

  Halfull_add1 halfull_add1_1 (.in_2(in_1), .in_3(in_5), .out_4(out_9), .out_5(halfull_add1_1_out_5));  // open: in_1
  Halfull_add1 halfull_add1_2 (
    .in_1(halfull_add1_1_out_5), .in_2(in_2), .in_3(in_6), .out_4(out_10), .out_5(halfull_add1_2_out_5));
  Halfull_add1 halfull_add1_3 (
    .in_1(halfull_add1_2_out_5), .in_2(in_3), .in_3(in_7), .out_4(out_11), .out_5(halfull_add1_3_out_5));
  Halfull_add1 halfull_add1_4 (.in_1(halfull_add1_3_out_5), .in_2(in_4), .in_3(in_8), .out_4(out_12), .out_5(out_13));
endmodule

module vision_example (
  input  in_1,
  input  in_2,
  input  in_3,
  input  in_4,
  input  in_5,
  input  in_6,
  input  in_7
);

  wire undriven, undriven_2, undriven_3, undriven_4, undriven_5, undriven_6, undriven_7;

  _7_Segment_Display u_7_segment_display_1 (
    .g(in_7), .f(in_6), .a(in_1), .b(in_2), .e(in_5), .d(in_4), .c(in_3), .dp(1'b1));
  _7_Segment_Display u_7_segment_display_2 (
    .g(undriven_3), .f(undriven_2), .a(undriven), .b(undriven_4), .e(undriven_5), .d(undriven_6),
    .c(undriven_7), .dp(1'b1));
endmodule

module sub4 (
  input  in_1,
  input  in_2,
  input  in_3,
  input  in_4,
  input  in_5,
  input  in_6,
  input  in_7,
  input  in_8,
  output out_9,
  output out_10,
  output out_11,
  output out_12,
  output out_13
);

  wire add4_1_out_9, add4_1_out_10, add4_1_out_11, add4_1_out_12, add4_1_out_13, add4_2_out_13, not_1_out,
       not_2_out, not_3_out, not_4_out, not_5_out, not_6_out;

  not not_1 (not_1_out, in_5);
  not not_2 (not_2_out, in_6);
  not not_3 (not_3_out, in_7);
  not not_4 (not_4_out, in_8);
  add4 add4_1 (
    .in_1(1'b1), .in_5(not_1_out), .in_6(not_2_out), .in_7(not_3_out), .in_8(not_4_out),
    .out_9(add4_1_out_9), .out_10(add4_1_out_10), .out_11(add4_1_out_11), .out_12(add4_1_out_12),
    .out_13(add4_1_out_13));  // open: in_2, in_3, in_4
  add4 add4_2 (
    .in_1(in_1), .in_2(in_2), .in_3(in_3), .in_4(in_4), .in_5(add4_1_out_9), .in_6(add4_1_out_10),
    .in_7(add4_1_out_11), .in_8(add4_1_out_12), .out_9(out_9), .out_10(out_10), .out_11(out_11),
    .out_12(out_12), .out_13(add4_2_out_13));
  not not_5 (not_5_out, add4_2_out_13);
  not not_6 (not_6_out, add4_1_out_13);
  and and_1 (out_13, not_5_out, not_6_out);
endmodule

module Self_XOR (
  input  in_1,
  input  in_2,
  input  in_3,
  input  in_4,
  input  in_5,
  input  in_6,
  output out_7,
  output out_8,
  output out_9
);

  wire and_1_out, and_2_out, and_3_out, and_4_out, nand_1_out, nand_2_out, not_1_out, not_2_out, or_1_out;

  not not_1 (not_1_out, in_6);
  not not_2 (not_2_out, in_5);
  or or_1 (or_1_out, in_2, in_1);
  nand nand_1 (nand_1_out, in_3, in_4);
  and and_1 (and_1_out, in_5, not_1_out);
  and and_2 (and_2_out, not_2_out, in_6);
  nand nand_2 (nand_2_out, in_1, in_2);
  and and_3 (and_3_out, in_3, nand_1_out);
  and and_4 (and_4_out, nand_1_out, in_4);
  or or_2 (out_9, and_1_out, and_2_out);
  and and_5 (out_7, or_1_out, nand_2_out);
  or or_3 (out_8, and_3_out, and_4_out);
endmodule

module register4 (
  input  in_1,
  input  in_2,
  input  in_3,
  input  in_4,
  input  in_5,
  input  in_6,
  input  in_7,
  output out_8,
  output out_9,
  output out_10,
  output out_11
);

  D_flipflop d_flipflop_1 (.in_1(in_2), .in_2(in_6), .in_3(in_1), .in_4(in_7), .out_5(out_8));  // open: out_6
  D_flipflop d_flipflop_2 (.in_1(in_3), .in_2(in_6), .in_3(in_1), .in_4(in_7), .out_5(out_9));  // open: out_6
  D_flipflop d_flipflop_3 (.in_1(in_4), .in_2(in_6), .in_3(in_1), .in_4(in_7), .out_5(out_10));  // open: out_6
  D_flipflop d_flipflop_4 (.in_1(in_5), .in_2(in_6), .in_3(in_1), .in_4(in_7), .out_5(out_11));  // open: out_6
endmodule

module D_flipflop_public (
  input  in_1,
  input  in_2,
  input  in_3,
  output out_4,
  output out_5
);

  wire and_1_out;

  and and_1 (and_1_out, in_1, in_2);
  D_Flip_Flop d_ff_1 (.D(and_1_out), .clk(in_3), .Q(out_4), .Qn(out_5));  // open: preset, reset
endmodule

module plusOne (
  input  in_1,
  input  [7:0] in_2,
  output [7:0] out_3,
  output out_4
);

  Adder adder_1 (.a(in_2), .b(8'h1), .out(out_3), .cin(in_1), .cout(out_4));
endmodule

module GaussianPlus (
  input  in_1,
  input  [7:0] in_2,
  input  in_3,
  output [7:0] out_4
);

  wire and_1_out, clock_1_out, clock_2_out, comparator_1_eq, comparator_1_gt, or_1_out;
  wire [7:0] adder_1_out, plusone_1_out_3, register_1_q, register_2_q;

  Clock clock_1 (.out(clock_1_out));
  Register register_1 (.D(plusone_1_out_3), .en(and_1_out), .clk(clock_1_out), .Q(register_1_q), .clr(in_3));
  plusOne plusone_1 (.in_2(register_1_q), .out_3(plusone_1_out_3));  // open: in_1, out_4
  Clock #(.phaseOffset(1)) clock_2 (.out(clock_2_out));
  Register register_2 (.D(out_4), .en(and_1_out), .clk(clock_2_out), .Q(register_2_q), .clr(in_3));
  or or_1 (or_1_out, comparator_1_gt, comparator_1_eq);
  Comparator comparator_1 (.a(in_2), .b(plusone_1_out_3), .gt(comparator_1_gt), .eq(comparator_1_eq));  // open: lt
  Adder adder_1 (.a(plusone_1_out_3), .b(register_2_q), .out(adder_1_out));  // open: cin, cout
  and and_1 (and_1_out, in_1, or_1_out);
  Register register_3 (.D(adder_1_out), .en(and_1_out), .clk(clock_1_out), .Q(out_4), .clr(in_3));
endmodule

module WhilePlus (
  input  [7:0] in_1,
  input  in_2,
  input  in_3,
  output [7:0] out_4
);

  wire comparator_1_eq, comparator_1_gt, or_1_out;
  wire [7:0] register_1_q;

  Comparator comparator_1 (.a(in_1), .b(out_4), .gt(comparator_1_gt), .eq(comparator_1_eq));  // open: lt
  Register register_1 (.D(out_4), .en(or_1_out), .clk(in_2), .Q(register_1_q), .clr(in_3));
  or or_1 (or_1_out, comparator_1_gt, comparator_1_eq);
  plusOne plusone_1 (.in_2(register_1_q), .out_3(out_4));  // open: in_1, out_4
endmodule
